// Logisim project Logisim的使用.circ as structural Verilog: 65 circuits, main circuit 电路封装
module \分线器  (
  input  [3:0] in_1,
  input  [3:0] in_2,
  input  [3:0] in_3,
  input  in_4,
  input  in_5,
  input  [7:0] in_6,
  input  in_7,
  input  in_8,
  output out_9,
  output out_10,
  output [7:0] out_11,
  output out_12,
  output out_13,
  output [3:0] out_14,
  output [3:0] out_15,
  output [3:0] out_16
);


  assign out_9 = in_2[0];
  assign out_10 = in_2[1];
  assign out_11 = {in_3, in_1};
  assign out_12 = in_2[2];
  assign out_13 = in_2[3];
  assign out_14 = in_6[3:0];
  assign out_15 = {in_8, in_7, in_5, in_4};
  assign out_16 = in_6[7:4];
endmodule

module \输入_输出  (
  input  in_1,
  output out_2
);
endmodule

module \探针  (
  input  A,
  input  B,
  output Y
);

  // Probe on A
  // Probe on B
  // Probe on Y
  xor xor_1 (Y, A, B);
endmodule

module \隧道  (
  input  in_1,
  input  in_2,
  output out_3
);

  and and_1 (out_3, in_1, in_2);

  // Other names for the same wires on the sheet: A = in_1; B = in_2; Y = out_3
endmodule

module \上拉电阻  (
  input  X,
  input  X_2,
  output Y,
  output Y_2
);

  wire pull_resistor_1_node, pull_resistor_2_node;

  Pull_Resistor pull_resistor_1 (.node(pull_resistor_1_node));
  Pull_Resistor #(.pull(1)) pull_resistor_2 (.node(pull_resistor_2_node));
  or or_1 (Y, X, pull_resistor_1_node);
  and and_1 (Y_2, X_2, pull_resistor_2_node);
endmodule

module \时钟  (
);

  wire CLK_out;

  Clock CLK (.out(CLK_out));
  LED LED (.in(CLK_out));
endmodule

module \函数发生器  (
  output out_1
);

  // ProgrammableGenerator #(.Contents("4 3 2 1 1 2 3 4")) programmablegenerator_1: pin names not known; wires that end beside it: out_1

  // Notes on the sheet:
  //   函数发生器
endmodule

module \常量  (
  input  A,
  input  B,
  output out_3,
  output Y
);

  // Probe on A
  // Probe on B
  and and_1 (out_3, 1'b1, 1'b0);
  // Probe on Y
  xor xor_1 (Y, A, B);
endmodule

module \电源_接地  (
  input  X,
  input  X_2,
  output Y,
  output Y_2
);

  or or_1 (Y, X, 1'b0);
  and and_1 (Y_2, X_2, 1'b1);
endmodule

module \传输门  (
  input  L,
  input  X,
  input  H,
  output Y
);

  // Transmission_Gate transmission_1: pin names not known; wires that end beside it: X, L, H, Y
endmodule

module \晶体管  (
  input  D,
  input  D_2,
  input  G,
  input  G_2,
  output S,
  output S_2
);

  Transistor transistor_1 (.in(D), .out(S), .gate(G));
  Transistor #(.\type ("n")) transistor_2 (.in(D_2), .out(S_2), .gate(G_2));
endmodule

module \位扩展器  (
  input  [7:0] in_1,
  input  [7:0] in_2,
  output [15:0] out_3,
  output [15:0] out_4
);

  assign out_3 = {{8{1'b0}}, in_1};  // Bit_Extender bit_extender_1
  assign out_4 = {{8{in_2[7]}}, in_2};  // Bit_Extender bit_extender_2
endmodule

module \非门  (
  input  A,
  output Y
);

  not not_1 (Y, A);
endmodule

module \缓冲器  (
  input  X,
  output Y
);

  buf buffer_1 (Y, X);
endmodule

module \与门  (
  input  A,
  input  B,
  output Y
);

  and and_1 (Y, A, B);
endmodule

module \或门  (
  input  A,
  input  B,
  output Y
);

  or or_1 (Y, A, B);
endmodule

module \与非门  (
  input  A,
  input  B,
  input  A_2,
  input  B_2,
  input  A_3,
  input  B_3,
  output Y,
  output Y_2,
  output Y_3
);

  wire not_1_out, not_2_out;

  nand nand_1 (Y, A, B);
  not not_1 (not_1_out, A_2);
  or or_1 (Y_2, not_1_out, not_2_out);
  not not_2 (not_2_out, B_2);
  or or_2 (Y_3, ~A_3, ~B_3);  // OR_Gate
endmodule

module \或非门  (
  input  A,
  input  B,
  input  A_2,
  input  B_2,
  input  A_3,
  input  B_3,
  output Y,
  output Y_2,
  output Y_3
);

  wire not_1_out, not_2_out;

  nor nor_1 (Y, A, B);
  not not_1 (not_1_out, A_2);
  not not_2 (not_2_out, B_2);
  and and_1 (Y_3, ~A_3, ~B_3);  // AND_Gate
  and and_2 (Y_2, not_1_out, not_2_out);
endmodule

module \异或门  (
  input  A,
  input  B,
  input  A_2,
  input  B_2,
  output Y,
  output Y_2
);

  wire and_1_out, and_2_out;

  xor xor_1 (Y, A, B);
  and and_1 (and_1_out, ~A_2, B_2);  // AND_Gate
  and and_2 (and_2_out, A_2, ~B_2);  // AND_Gate
  or or_1 (Y_2, and_1_out, and_2_out);
endmodule

module \异或非门  (
  input  A,
  input  B,
  input  A_2,
  input  B_2,
  output Y,
  output Y_2
);

  wire and_1_out, and_2_out;

  xnor xnor_1 (Y, A, B);
  and and_1 (and_1_out, A_2, B_2);
  and and_2 (and_2_out, ~A_2, ~B_2);  // AND_Gate
  or or_1 (Y_2, and_1_out, and_2_out);
endmodule

module \奇校验  (
  input  A,
  input  B,
  output Y
);

  xor odd_parity_1 (Y, A, B);

  // Notes on the sheet:
  //   奇校验（Odd Parity）
endmodule

module \偶校验  (
  input  A,
  input  B,
  output Y
);

  xnor even_parity_1 (Y, A, B);

  // Notes on the sheet:
  //   偶校验（Even Parity）
endmodule

module \可控缓冲器  (
  input  X,
  input  C,
  output Y
);

  assign Y = C ? X : 1'bz;  // Controlled_Buffer controlled_buffer_1
endmodule

module \可控反相器  (
  input  X,
  input  C,
  output Y
);

  assign Y = C ? ~X : 1'bz;  // Controlled_Inverter controlled_inverter_1
endmodule

module _7400 (
  input  A,
  input  B,
  output Y,
  output Y_2
);

  // _7400_part 7400_1: pin names not known; wires that end beside it: 1'b1, A, B, Y, 1'b0
  nand nand_1 (Y_2, A, B);

  // Notes on the sheet:
  //   4个与非门
endmodule

module _7402 (
  input  A,
  input  B,
  output Y,
  output Y_2
);

  // _7402_part 7402_1: pin names not known; wires that end beside it: 1'b1, A, B, Y, 1'b0
  nor nor_1 (Y_2, A, B);

  // Notes on the sheet:
  //   4个或非门
endmodule

module _7404 (
  input  A,
  output Y,
  output Y_2
);

  // _7404_part 7404_1: pin names not known; wires that end beside it: 1'b1, A, Y, 1'b0
  not not_1 (Y_2, A);

  // Notes on the sheet:
  //   6个非门
endmodule

module _7408 (
  input  A,
  input  B,
  output Y,
  output Y_2
);

  // _7408_part 7408_1: pin names not known; wires that end beside it: 1'b1, A, B, Y, 1'b0
  and and_1 (Y_2, A, B);

  // Notes on the sheet:
  //   4个与门
endmodule

module _7432 (
  input  A,
  input  B,
  output Y,
  output Y_2
);

  // _7432_part 7432_1: pin names not known; wires that end beside it: 1'b1, A, B, Y, 1'b0
  or or_1 (Y_2, A, B);

  // Notes on the sheet:
  //   4个或门
endmodule

module _7447 (
  input  [3:0] A,
  input  LT,
  input  BI,
  input  RBI,
  output [6:0] Y
);

  _7447_part u_7447_1 (
    .pin1(A[1]), .pin2(A[2]), .pin3(LT), .pin4(BI), .pin5(RBI), .pin6(A[3]), .pin7(A[0]), .pin15(Y[6]),
    .pin14(Y[5]), .pin13(Y[4]), .pin12(Y[3]), .pin11(Y[2]), .pin10(Y[1]), .pin9(Y[0]));
  _7_Segment_Display u_7_segment_display_1 (
    .g(Y[5]), .f(Y[6]), .a(Y[4]), .b(Y[3]), .e(Y[0]), .d(Y[1]), .c(Y[2]), .dp(1'b0));

  // Notes on the sheet:
  //   7段码译码器
  //   数码管
endmodule

module _7485 (
  input  [3:0] A,
  input  [3:0] B,
  input  A_B,
  input  A_B_2,
  input  A_B_3,
  output A_B_4,
  output A_B_5,
  output A_B_6
);

  _7485_part u_7485_1 (
    .pin1(B[3]), .pin2(A_B), .pin3(A_B_2), .pin4(A_B_3), .pin5(A_B_6), .pin6(A_B_5), .pin7(A_B_4),
    .pin15(A[3]), .pin14(B[2]), .pin13(A[2]), .pin12(A[1]), .pin11(B[1]), .pin10(A[0]), .pin9(B[0]));

  // Notes on the sheet:
  //   4位比较器
endmodule

module _7486 (
  input  A,
  input  B,
  output Y,
  output Y_2
);

  // _7486_part 7486_1: pin names not known; wires that end beside it: 1'b1, A, B, Y, 1'b0
  xor xor_1 (Y_2, A, B);

  // Notes on the sheet:
  //   4个异或门
endmodule

module _74125 (
  input  C,
  input  X,
  output Y
);


  // Notes on the sheet:
  //   4个三态门
endmodule

module _74165 (
  input  Serial_Input,
  input  Clk_Inhibit,
  input  [7:0] Data,
  input  Shift_Load,
  output Q7,
  output nQ7
);

  wire CLK_out;

  Button CLK (.out(CLK_out));
  _74165_part u_74165_1 (
    .pin1(Shift_Load), .pin2(CLK_out), .pin3(Data[4]), .pin4(Data[5]), .pin5(Data[6]), .pin6(Data[7]),
    .pin7(nQ7), .pin15(Clk_Inhibit), .pin14(Data[3]), .pin13(Data[2]), .pin12(Data[1]), .pin11(Data[0]),
    .pin10(Serial_Input), .pin9(Q7));

  // Notes on the sheet:
  //   8位并-串转换移位寄存器
endmodule

module _74283 (
  input  [3:0] A,
  input  [3:0] B,
  input  Cin,
  output Cout,
  output [3:0] C
);

  _74283_part u_74283_1 (
    .pin1(C[1]), .pin2(B[1]), .pin3(A[1]), .pin4(C[0]), .pin5(A[0]), .pin6(B[0]), .pin7(Cin), .pin15(B[2]),
    .pin14(A[2]), .pin13(C[2]), .pin12(A[3]), .pin11(B[3]), .pin10(C[3]), .pin9(Cout));

  // Notes on the sheet:
  //   4位加法器
endmodule

module _747266 (
  input  A,
  input  B,
  output Y,
  output Y_2
);

  // _747266_part 747266_1: pin names not known; wires that end beside it: 1'b1, A, B, Y, 1'b0
  xnor xnor_1 (Y_2, A, B);

  // Notes on the sheet:
  //   4个异或非门
endmodule

module \多路选择器  (
  input  A,
  input  B,
  input  SEL,
  input  A_2,
  input  B_2,
  input  C,
  input  D,
  input  [1:0] SEL_2,
  output Y,
  output Y_2
);

  Multiplexer #(.enable("false")) multiplexer_1 (.in0(A), .in1(B), .out(Y), .sel(SEL));
  Multiplexer #(.select(2), .enable("false")) multiplexer_2 (
    .in0(A_2), .in1(B_2), .in2(C), .in3(D), .out(Y_2), .sel(SEL_2));
endmodule

module \多路分配器  (
  input  X,
  input  SEL,
  input  X_2,
  input  [1:0] SEL_2,
  output Y0,
  output Y1,
  output Y0_2,
  output Y1_2,
  output Y2,
  output Y3
);

  Demultiplexer #(.enable("false")) demultiplexer_1 (.out0(Y0), .out1(Y1), .in(X), .sel(SEL));
  Demultiplexer #(.select(2), .enable("false")) demultiplexer_2 (
    .out0(Y0_2), .out1(Y1_2), .out2(Y2), .out3(Y3), .in(X_2), .sel(SEL_2));
endmodule

module \解码器  (
  input  SEL,
  input  SEL_2,
  input  A2,
  input  A1,
  input  A0,
  input  [1:0] SEL_3,
  output Y0,
  output Y0_2,
  output Y1,
  output Y1_2,
  output Y2,
  output Y3,
  output Y4,
  output Y5,
  output Y6,
  output Y0_3,
  output Y7,
  output Y1_3,
  output Y2_2,
  output Y3_2
);

  Decoder #(.enable("false")) decoder_1 (.out0(Y0), .out1(Y1), .sel(SEL));
  Decoder #(.select(2), .enable("false")) decoder_2 (.out0(Y0_3), .out1(Y1_3), .out2(Y2_2), .out3(Y3_2), .sel(SEL_3));
  Decoder #(.select(3), .disabled(0)) decoder_3 (
    .out0(Y0_2), .out1(Y1_2), .out2(Y2), .out3(Y3), .out4(Y4), .out5(Y5), .out6(Y6), .out7(Y7),
    .sel({A2, A1, A0}), .en(SEL_2));
endmodule

module \七段码解码器  (
  input  EI,
  input  [3:0] Data,
  input  LT,
  input  BI,
  input  RBI,
  input  DP,
  output [6:0] Seg
);

  // Probe on Data
  // DisplayDecoder displaydecoder_1: pin names not known; wires that end beside it: Data, LT, EI, BI, RBI, Seg[0], Seg[1], Seg[2], Seg[3], Seg[4], Seg[5], Seg[6]
  _7_Segment_Display u_7_segment_display_1 (
    .g(Seg[6]), .f(Seg[5]), .a(Seg[0]), .b(Seg[1]), .e(Seg[4]), .d(Seg[3]), .c(Seg[2]), .dp(DP));
  // Probe on Seg
endmodule

module \优先级编码器  (
  input  In0,
  input  In1,
  input  In2,
  input  In3,
  input  In4,
  input  In5,
  input  In6,
  input  In7,
  input  EN,
  output EO,
  output [2:0] O,
  output GS
);

  Priority_Encoder priority_encoder_1 (
    .in0(In0), .in1(In1), .in2(In2), .in3(In3), .in4(In4), .in5(In5), .in6(In6), .in7(In7), .out(O), .gs(GS),
    .en_out(EO), .en_in(EN));
endmodule

module \位选择器  (
  input  [7:0] X,
  input  [2:0] SEL,
  output Y
);

  BitSelector bitselector_1 (.in(X), .out(Y), .sel(SEL));
endmodule

module \加法器  (
  input  Cin,
  input  [7:0] A,
  input  [7:0] B,
  input  Cin_2,
  input  [7:0] A_2,
  input  [7:0] B_2,
  output [7:0] Y,
  output Cout,
  output [7:0] Y_2,
  output Cout_2
);

  // Probe on A
  // Probe on B
  // Probe on A_2
  // Probe on B_2
  // Probe on Y
  Adder adder_1 (.a(A), .b(B), .out(Y), .cin(Cin), .cout(Cout));
  // Probe on Y_2
  Adder adder_2 (.a(A_2), .b(B_2), .out(Y_2), .cin(Cin_2), .cout(Cout_2));
endmodule

module \减法器  (
  input  Cin,
  input  [7:0] A,
  input  [7:0] B,
  input  Cin_2,
  input  [7:0] A_2,
  input  [7:0] B_2,
  output [7:0] Y,
  output Cout,
  output [7:0] Y_2,
  output Cout_2
);

  // Probe on A
  // Probe on B
  // Probe on A_2
  // Probe on B_2
  // Probe on Y
  Subtractor subtractor_1 (.a(A), .b(B), .out(Y), .bin(Cin), .bout(Cout));
  // Probe on Y_2
  Subtractor subtractor_2 (.a(A_2), .b(B_2), .out(Y_2), .bin(Cin_2), .bout(Cout_2));
endmodule

module \乘法器  (
  input  [7:0] C,
  input  [7:0] A,
  input  [7:0] B,
  output [7:0] Y0,
  output [15:0] Y,
  output [7:0] Y1
);

  // Probe on C
  // Probe on A
  // Probe on B
  Multiplier multiplier_1 (.a(A), .b(B), .out(Y[7:0]), .cin(C), .cout(Y[15:8]));
  // Probe on Y

  assign Y0 = Y[7:0];
  assign Y1 = Y[15:8];
endmodule

module \除法器  (
  input  [15:0] A,
  input  [7:0] B,
  output [7:0] Q,
  output [7:0] R
);

  // Probe on A
  // Probe on B
  Divider divider_1 (.a(A[7:0]), .b(B), .out(Q), .upper(A[15:8]), .rem(R));
  // Probe on Q
  // Probe on R
endmodule

module \求补器  (
  input  [7:0] X,
  input  [7:0] X_2,
  output [7:0] Y,
  output [7:0] Y_2
);

  // Probe on X
  // Probe on X_2
  // Probe on Y
  Negator negator_1 (.in(X), .out(Y));
  // Probe on Y_2
  Negator negator_2 (.in(X_2), .out(Y_2));
endmodule

module \比较器  (
  input  [7:0] in_1,
  input  [7:0] in_2,
  input  [7:0] in_3,
  input  [7:0] in_4,
  input  [7:0] in_5,
  input  [7:0] in_6,
  input  [7:0] in_7,
  input  [7:0] in_8,
  input  [7:0] in_9,
  input  [7:0] in_10,
  input  [7:0] in_11,
  input  [7:0] in_12,
  output out_13,
  output out_14,
  output out_15,
  output out_16,
  output out_17,
  output out_18,
  output out_19,
  output out_20,
  output out_21,
  output out_22,
  output out_23,
  output out_24,
  output out_25,
  output out_26,
  output out_27,
  output out_28,
  output out_29,
  output out_30
);

  // Probe on in_1
  // Probe on in_3
  // Probe on in_5
  // Probe on in_7
  // Probe on in_10
  // Probe on in_12
  Comparator comparator_1 (.a(in_1), .b(in_3), .gt(out_13), .eq(out_15), .lt(out_17));
  Comparator comparator_2 (.a(in_5), .b(in_7), .gt(out_19), .eq(out_21), .lt(out_23));
  Comparator comparator_3 (.a(in_10), .b(in_12), .gt(out_26), .eq(out_28), .lt(out_30));
  // Probe on in_2
  // Probe on in_4
  // Probe on in_6
  // Probe on in_8
  // Probe on in_9
  // Probe on in_11
  Comparator comparator_4 (.a(in_2), .b(in_4), .gt(out_14), .eq(out_16), .lt(out_18));
  Comparator comparator_5 (.a(in_6), .b(in_8), .gt(out_20), .eq(out_22), .lt(out_24));
  Comparator comparator_6 (.a(in_9), .b(in_11), .gt(out_25), .eq(out_27), .lt(out_29));
endmodule

module \移位器  (
  input  [7:0] X,
  input  [7:0] X_2,
  input  [2:0] S,
  input  [2:0] S_2,
  input  [7:0] X_3,
  input  [7:0] X_4,
  input  [2:0] S_3,
  input  [2:0] S_4,
  input  [7:0] X_5,
  input  [2:0] S_5,
  output [7:0] Y,
  output [7:0] Y_2,
  output [7:0] Y_3,
  output [7:0] Y_4,
  output [7:0] Y_5
);

  Shifter shifter_1 (.in(X), .\dist (S), .out(Y));
  Shifter #(.shift("lr")) shifter_2 (.in(X_3), .\dist (S_3), .out(Y_3));
  Shifter #(.shift("ar")) shifter_3 (.in(X_5), .\dist (S_5), .out(Y_5));
  Shifter #(.shift("rl")) shifter_4 (.in(X_2), .\dist (S_2), .out(Y_2));
  Shifter #(.shift("rr")) shifter_5 (.in(X_4), .\dist (S_4), .out(Y_4));

  // Notes on the sheet:
  //   逻辑左移
  //   逻辑右移
  //   算术右移
  //   循环左移
  //   循环右移
endmodule

module \位加法器  (
  input  [7:0] X,
  output [3:0] Y
);

  BitAdder bitadder_1 (.in0(X), .out(Y));
endmodule

module \位发现器  (
  input  [7:0] X,
  input  [7:0] X_2,
  output [2:0] Y,
  output [2:0] Y_2,
  output S,
  output S_2
);

  BitFinder bitfinder_1 (.in(X), .index(Y), .found(S));
  BitFinder bitfinder_2 (.in(X_2), .index(Y_2), .found(S_2));
endmodule

module \D触发器  (
  input  Set,
  input  D,
  input  Clr,
  output Q,
  output nQ
);

  wire CLK_out;

  Button CLK (.out(CLK_out));
  D_Flip_Flop d_ff_1 (.clk(CLK_out), .D(D), .Q(Q), .Qn(nQ), .preset(Set), .reset(Clr));
endmodule

module \T触发器  (
  input  Set,
  input  T,
  input  Clr,
  output Q,
  output nQ
);

  wire CLK_out;

  Button CLK (.out(CLK_out));
  T_Flip_Flop t_ff_1 (.clk(CLK_out), .T(T), .Q(Q), .Qn(nQ), .preset(Set), .reset(Clr));
endmodule

module \J_K_触发器  (
  input  Set,
  input  J,
  input  K,
  input  Clr,
  output Q,
  output nQ
);

  wire CLK_out;

  Button CLK (.out(CLK_out));
  J_K_Flip_Flop j_k_ff_1 (.J(J), .clk(CLK_out), .K(K), .Q(Q), .Qn(nQ), .preset(Set), .reset(Clr));
endmodule

module \S_R_触发器  (
  input  Set,
  input  S,
  input  R,
  input  Clr,
  output Q,
  output nQ
);

  wire CLK_out;

  Button CLK (.out(CLK_out));
  S_R_Flip_Flop s_r_ff_1 (.S(S), .clk(CLK_out), .R(R), .Q(Q), .Qn(nQ), .preset(Set), .reset(Clr));
endmodule

module \寄存器  (
  input  Set,
  input  CS,
  input  [7:0] D,
  input  EN,
  input  Clr,
  output [7:0] Q
);

  wire CLK_out;

  Button CLK (.out(CLK_out));
  Register #(.Select("low")) register_1 (.D(D), .en(EN), .Q(Q), .clk(CLK_out), .clr(Clr), .cs(CS), .preset(Set));
endmodule

module \计数器  (
  input  Set,
  input  EN,
  input  Load,
  input  [7:0] D,
  input  Rever,
  input  Clr,
  output [7:0] Q
);

  wire CLK_out;

  Button CLK (.out(CLK_out));
  Counter counter_1 (
    .load(Load), .D(D), .count(EN), .Q(Q), .clk(CLK_out), .clr(Clr), .preset(Set), .down(Rever));  // open: carry
endmodule

module \移位寄存器  (
  input  [7:0] D,
  input  Load,
  input  Shift,
  input  Input,
  input  Clr,
  output Q0,
  output [7:0] Q
);

  wire CLK_out;

  Button CLK (.out(CLK_out));
  Shift_Register shift_register_1 (
    .shift(Shift), .in(Input), .clk(CLK_out), .out(Q0), .load(Load), .clr(Clr), .d0(D[7]), .q0(Q[7]),
    .d1(D[6]), .q1(Q[6]), .d2(D[6]), .q2(Q[5]), .d3(D[4]), .q3(Q[4]), .d4(D[3]), .q4(Q[3]), .d5(D[2]),
    .q5(Q[2]), .d6(D[1]), .q6(Q[1]), .d7(D[0]), .q7(Q[0]));

  assign D[5] = D[6];
endmodule

module \随机数发生器  (
  input  EN,
  input  Clr,
  output [7:0] Q
);

  wire CLK_out;

  Button CLK (.out(CLK_out));
  Random random_1 (.clk(CLK_out), .next(EN), .out(Q), .clr(Clr));
  // Probe on Q
endmodule

module RAM (
  input  [7:0] A,
  input  Sel,
  input  Load,
  input  Clr,
  input  [7:0] A_2,
  input  Sel_2,
  input  Load_2,
  input  Clr_2,
  input  [7:0] A_3,
  input  [31:0] Din,
  input  Str,
  input  Sel_3,
  input  Load_3,
  input  Clr_3,
  output [31:0] D,
  output [31:0] D_2,
  output [31:0] Dout
);

  wire CLK_2_out, CLK_out;

  Button CLK (.out(CLK_out));
  Button CLK_2 (.out(CLK_2_out));
  RAM_part #(.dataWidth(32), .Select("low")) ram_1 (.addr(A), .data(D), .sel(Sel), .clk(CLK_out), .ld(Load), .clr(Clr));
  RAM_part #(.dataWidth(32), .bus("asynch"), .Select("low")) ram_2 (
    .addr(A_2), .data(D_2), .sel(Sel_2), .ld(Load_2), .clr(Clr_2));
  RAM_part #(.dataWidth(32), .bus("separate"), .Select("low")) ram_3 (
    .addr(A_3), .din(Din), .data(Dout), .str(Str), .sel(Sel_3), .clk(CLK_2_out), .ld(Load_3), .clr(Clr_3));
endmodule

module ROM (
  input  [7:0] A,
  input  Sel,
  output [31:0] D
);

  ROM_part #(.dataWidth(32), .Select("low")) rom_1 (.addr(A), .data(D), .sel(Sel));

  // Notes on the sheet:
  //   contents of rom_1 (hex, n*v repeats v):
  //   11111111 22222222 33333333 44444444 55555555 66666666 77777777 88888888 99999999 aaaaaaaa bbbbbbbb
  //   cccccccc dddddddd eeeeeeee ffffffff
endmodule

module PLA__ROM (
  input  [3:0] A,
  input  Sel,
  output [3:0] D
);

  // PlaRom #(.Contents("2*16 1*16")) plarom_1: pin names not known; wires that end beside it: A, Sel, D
endmodule

module \输入_输出部件  (
  input  in_1,
  input  [13:0] Fre,
  input  EN,
  input  EN_2,
  input  Clr,
  input  [6:0] Vol,
  input  R,
  input  G,
  input  B,
  input  IN1,
  input  [3:0] in_11,
  input  IN2,
  input  IN3,
  input  EN_3,
  input  DP,
  input  Clr_2,
  input  [6:0] in_17,
  input  [6:0] in_18,
  input  [6:0] in_19,
  input  [3:0] in_20,
  input  DP_2,
  input  [6:0] in_22,
  input  [6:0] in_23,
  input  [6:0] Data,
  input  EN_4,
  input  Clr_3,
  input  [31:0] in_27,
  input  [31:0] in_28,
  input  [31:0] in_29,
  input  [31:0] in_30,
  input  [31:0] in_31,
  input  [31:0] in_32,
  input  [31:0] in_33,
  input  [31:0] in_34,
  input  [31:0] in_35,
  input  [31:0] in_36,
  input  [31:0] in_37,
  input  [31:0] in_38,
  input  [31:0] in_39,
  input  [31:0] in_40,
  input  [31:0] in_41,
  input  [31:0] in_42,
  input  [31:0] in_43,
  input  [31:0] in_44,
  input  [31:0] in_45,
  input  [31:0] in_46,
  input  [31:0] in_47,
  input  [31:0] in_48,
  input  [31:0] in_49,
  input  [31:0] in_50,
  input  [31:0] in_51,
  input  [31:0] in_52,
  input  [31:0] in_53,
  input  [31:0] in_54,
  input  [31:0] in_55,
  input  [31:0] in_56,
  input  [31:0] in_57,
  input  [31:0] in_58,
  output out_59,
  output [3:0] out_60,
  output [3:0] out_61,
  output [7:0] out_62,
  output [3:0] out_63,
  output [6:0] Data_2,
  output Avai
);

  wire CLK_2_out, CLK_3_out, CLK_out, displaydecoder_1_p2, displaydecoder_1_p3, displaydecoder_1_p4,
       displaydecoder_1_p5, displaydecoder_1_p6, displaydecoder_1_p7, displaydecoder_1_p8, \按钮_Button_2_out ,
       \按钮_Button_out ;

  Button CLK (.out(CLK_out));
  Button \u_按钮_Button  (.out(\按钮_Button_out ));
  Keyboard keyboard_1 (.clk(CLK_out), .re(EN_2), .clr(Clr), .avail(Avai), .data(Data_2));
  Button \u_按钮_Button_2  (.out(\按钮_Button_2_out ));
  Button CLK_2 (.out(CLK_2_out));
  Button CLK_3 (.out(CLK_3_out));
  // Probe on \按钮_Button_out 
  Slider #(.value('h6b)) slider_1 (.out(out_62));
  // Probe on \按钮_Button_2_out 
  // Digital_Oscilloscope 数字示波器_Digital_Oscilloscope: pin names not known; wires that end beside it: CLK_2_out, IN1, IN2, IN3, EN_3, Clr_2
  LED LED (.in(\按钮_Button_out ));
  // Probe on Data_2
  LED LED_2 (.in(\按钮_Button_2_out ));
  Hex_Digit_Display hex_digit_display_1 (.value(in_20), .dp(DP_2));
  TTY tty_1 (.data(Data), .clk(CLK_3_out), .we(EN_4), .clr(Clr_3));
  // Switch 开关_Switch: pin names not known; wires that end beside it: in_1, out_59
  Joystick joystick_1 (.x(out_61), .y(out_63));
  // RGBLed RGB_LED: pin names not known; wires that end beside it: R, G, B
  // Probe on in_11
  // Buzzer 蜂鸣器_Buzzer: pin names not known; wires that end beside it: Fre, EN, Vol
  // DisplayDecoder displaydecoder_1: pin names not known; wires that end beside it: in_11, displaydecoder_1_p2, displaydecoder_1_p3, displaydecoder_1_p4, displaydecoder_1_p5, displaydecoder_1_p6, displaydecoder_1_p7, displaydecoder_1_p8
  DotMatrix #(.matrixcols(32), .matrixrows(32)) dotmatrix_1 (
    .col0(in_27), .col1(in_28), .col2(in_29), .col3(in_30), .col4(in_31), .col5(in_32), .col6(in_33),
    .col7(in_34), .col8(in_35), .col9(in_36), .col10(in_37), .col11(in_38), .col12(in_39), .col13(in_40),
    .col14(in_41), .col15(in_42), .col16(in_43), .col17(in_44), .col18(in_45), .col19(in_46), .col20(in_47),
    .col21(in_48), .col22(in_49), .col23(in_50), .col24(in_51), .col25(in_52), .col26(in_53), .col27(in_54),
    .col28(in_55), .col29(in_56), .col30(in_57), .col31(in_58));
  // DipSwitch dipswitch_1: pin names not known; wires that end beside it: out_60[0], out_60[1], out_60[2], out_60[3]
  _7_Segment_Display u_7_segment_display_1 (
    .g(displaydecoder_1_p8), .f(displaydecoder_1_p7), .a(displaydecoder_1_p2), .b(displaydecoder_1_p3),
    .e(displaydecoder_1_p6), .d(displaydecoder_1_p5), .c(displaydecoder_1_p4), .dp(DP));
  DotMatrix dotmatrix_2 (.col0(in_17), .col1(in_18), .col2(in_19), .col3(in_22), .col4(in_23));

  // Notes on the sheet:
  //   滑杆（Slider）
  //   键盘（Keyboard）
  //   十六进制数码管（Hex Digital Display）
  //   终端（TTY）
  //   游戏杆（Joystick）
  //   七段码解码器
  //   DIP开关（DIP Switch）
  //   LED点阵（LED Matrix）
  //   LED点阵（LED Matrix）
  //   数码管（7-Segment Display）
endmodule

module \电路封装  (
  input  A,
  input  B,
  input  in_3,
  output Y,
  output out_5
);

  wire and_1_out, and_2_out, not_1_out, not_2_out, \分线器_1_out_10 ;

  not not_1 (not_1_out, B);
  not not_2 (not_2_out, A);
  \常量  \u_常量_1  ();  // open: A, B, out_3, Y
  \隧道  \u_隧道_1  ();  // open: in_1, in_2, out_3
  \电源_接地  \u_电源_接地_1  ();  // open: X, X_2, Y, Y_2
  \多路选择器  \u_多路选择器_1  ();  // open: A, B, SEL, A_2, B_2, C, D, SEL_2, Y, Y_2
  \加法器  \u_加法器_1  ();  // open: Cin, A, B, Cin_2, A_2, B_2, Y, Cout, Y_2, Cout_2
  \D触发器  \d触发器_1  ();  // open: Set, D, Clr, Q, nQ
  and and_1 (and_1_out, not_1_out, A);
  and and_2 (and_2_out, B, not_2_out);
  \晶体管  \u_晶体管_1  ();  // open: G, G_2, D, D_2, S, S_2
  \非门  \u_非门_1  ();  // open: A, Y
  \缓冲器  \u_缓冲器_1  ();  // open: X, Y
  _7400 u_7400_1 ();  // open: A, B, Y, Y_2
  \多路分配器  \u_多路分配器_1  ();  // open: X, SEL, X_2, SEL_2, Y0, Y1, Y0_2, Y1_2, Y2, Y3
  \减法器  \u_减法器_1  ();  // open: Cin, A, B, Cin_2, A_2, B_2, Y, Cout, Y_2, Cout_2
  \乘法器  \u_乘法器_1  ();  // open: C, A, B, Y0, Y, Y1
  \T触发器  \t触发器_1  ();  // open: Set, T, Clr, Q, nQ
  or or_1 (Y, and_1_out, and_2_out);
  \分线器  \u_分线器_1  (.out_10(\分线器_1_out_10 ));  // open: in_1, in_2, in_3, in_4, in_5, in_6, in_7, in_8, out_9, out_11, out_12, out_13, out_14, out_15, out_16
  \传输门  \u_传输门_1  ();  // open: X, L, H, Y
  \与门  \u_与门_1  ();  // open: A, B, Y
  \或门  \u_或门_1  ();  // open: A, B, Y
  _7404 u_7404_1 ();  // open: A, Y, Y_2
  _7402 u_7402_1 ();  // open: A, B, Y, Y_2
  \求补器  \u_求补器_1  ();  // open: X, X_2, Y, Y_2
  \除法器  \u_除法器_1  ();  // open: A, B, Q, R
  \J_K_触发器  \j_k_触发器_1  ();  // open: Set, J, K, Clr, Q, nQ
  \S_R_触发器  \s_r_触发器_1  ();  // open: Set, S, R, Clr, Q, nQ
  \输入_输出  \u_输入_输出_1  (.in_1(\分线器_1_out_10 ));  // open: out_2
  \探针  \u_探针_1  ();  // open: A, B, Y
  \位扩展器  \u_位扩展器_1  ();  // open: in_1, in_2, out_3, out_4
  \与非门  \u_与非门_1  ();  // open: A, B, A_2, B_2, A_3, B_3, Y, Y_2, Y_3
  _7432 u_7432_1 ();  // open: A, B, Y, Y_2
  _7408 u_7408_1 ();  // open: A, B, Y, Y_2
  \解码器  \u_解码器_1  ();  // open: SEL_2, SEL, SEL_3, A2, A1, A0, Y0, Y0_2, Y1, Y1_2, Y2, Y3, Y4, Y5, Y6, Y0_3, Y7, Y1_3, Y2_2, Y3_2
  \比较器  \u_比较器_1  ();  // open: in_1, in_2, in_3, in_4, in_5, in_6, in_7, in_8, in_9, in_10, in_11, in_12, out_13, out_14, out_15, out_16, out_17, out_18, out_19, out_20, out_21, out_22, out_23, out_24, out_25, out_26, out_27, out_28, out_29, out_30
  \寄存器  \u_寄存器_1  ();  // open: Set, CS, D, EN, Clr, Q
  \计数器  \u_计数器_1  ();  // open: Set, EN, Load, D, Rever, Clr, Q
  \上拉电阻  \u_上拉电阻_1  ();  // open: X, X_2, Y, Y_2
  \时钟  \u_时钟_1  ();
  \或非门  \u_或非门_1  ();  // open: A, B, A_2, B_2, A_3, B_3, Y, Y_2, Y_3
  \异或门  \u_异或门_1  ();  // open: A, B, A_2, B_2, Y, Y_2
  _7485 u_7485_1 ();  // open: A, B, A_B, A_B_2, A_B_3, A_B_4, A_B_5, A_B_6
  _7447 u_7447_1 ();  // open: A, LT, BI, RBI, Y
  \七段码解码器  \u_七段码解码器_1  ();  // open: EI, Data, LT, BI, RBI, DP, Seg
  \移位器  \u_移位器_1  ();  // open: X, X_2, S, S_2, X_3, X_4, S_3, S_4, X_5, S_5, Y, Y_2, Y_3, Y_4, Y_5
  \位加法器  \u_位加法器_1  ();  // open: X, Y
  \移位寄存器  \u_移位寄存器_1  ();  // open: D, Load, Shift, Input, Clr, Q0, Q
  \随机数发生器  \u_随机数发生器_1  ();  // open: EN, Clr, Q
  \异或非门  \u_异或非门_1  ();  // open: A, B, A_2, B_2, Y, Y_2
  _7486 u_7486_1 ();  // open: A, B, Y, Y_2
  \优先级编码器  \u_优先级编码器_1  ();  // open: In0, In1, In2, In3, In4, In5, In6, In7, EN, EO, O, GS
  \位发现器  \u_位发现器_1  ();  // open: X, X_2, Y, Y_2, S, S_2
  RAM ram_1 ();  // open: A, Sel, Load, Clr, A_2, Sel_2, Load_2, Clr_2, A_3, Din, Str, Sel_3, Load_3, Clr_3, D, D_2, Dout
  \偶校验  \u_偶校验_1  ();  // open: A, B, Y
  \奇校验  \u_奇校验_1  ();  // open: A, B, Y
  _74283 u_74283_1 ();  // open: A, B, Cin, Cout, C
  _74165 u_74165_1 ();  // open: Serial_Input, Clk_Inhibit, Data, Shift_Load, Q7, nQ7
  \位选择器  \u_位选择器_1  ();  // open: X, SEL, Y
  ROM rom_1 ();  // open: A, Sel, D
  \可控反相器  \u_可控反相器_1  ();  // open: X, C, Y
  \可控缓冲器  \u_可控缓冲器_1  ();  // open: X, C, Y
  _747266 u_747266_1 ();  // open: A, B, Y, Y_2

  // Notes on the sheet:
  //   异或门
  //   Y = A 异或 B
endmodule

module \电路封装的应用  (
  input  A,
  input  B,
  output Y
);

  \电路封装  \u_异或门  (.A(A), .B(B), .Y(Y));  // open: in_3, out_5
endmodule
