// Logisim project cache 挑战实验.circ as structural Verilog: 4 circuits, main circuit cache（直接相联映射）电路（16个cache块）
// 直接相联cache
module \cache_直接相联映射_电路_16个cache块  (
  input  [15:0] Addr,
  input  [31:0] BlockDataIn,
  input  BlkDataReady,
  input  CLK,
  output Miss,
  output [7:0] DataOut
);

  wire and_2_out, and_3_out, and_4_out, and_5_out, and_6_out, and_7_out, and_8_out, and_9_out, and_10_out,
       and_11_out, and_12_out, and_13_out, and_14_out, and_15_out, and_16_out, and_17_out, comparator_1_eq,
       Hit, L0, L1, L2, L3, L4, L5, L6, L7, L8, L9, L10, L11, L12, L13, L14, L15, Valid, VALID_2_q,
       VALID_3_q, VALID_4_q, VALID_5_q, VALID_6_q, VALID_7_q, VALID_8_q, VALID_9_q, VALID_10_q, VALID_11_q,
       VALID_12_q, VALID_13_q, VALID_14_q, VALID_15_q, VALID_16_q, VALID_q;
  wire [9:0] TAG_2_q, TAG_3_q, TAG_4_q, TAG_5_q, TAG_6_q, TAG_7_q, TAG_8_q, TAG_9_q, TAG_10_q, TAG_11_q,
       TAG_12_q, TAG_13_q, TAG_14_q, TAG_15_q, TAG_16_q, TAG_q, TagData;
  wire [31:0] DATA_COPY_2_q, DATA_COPY_3_q, DATA_COPY_4_q, DATA_COPY_5_q, DATA_COPY_6_q, DATA_COPY_7_q,
       DATA_COPY_8_q, DATA_COPY_q, SlotData, \数据块副本_2_q , \数据块副本_3_q , \数据块副本_4_q , \数据块副本_5_q , \数据块副本_6_q ,
       \数据块副本_7_q , \数据块副本_8_q , \数据块副本_q ;

  Register #(.width(1), .Select("low")) u_VALID (.D(1'b1), .en(and_2_out), .Q(VALID_q), .clk(CLK));  // open: clr
  Register #(.width(1), .Select("low")) VALID_2 (.D(1'b1), .en(and_3_out), .Q(VALID_2_q), .clk(CLK));  // open: clr
  Register #(.width(1), .Select("low")) VALID_3 (.D(1'b1), .en(and_4_out), .Q(VALID_3_q), .clk(CLK));  // open: clr
  Register #(.width(1), .Select("low")) VALID_4 (.D(1'b1), .en(and_5_out), .Q(VALID_4_q), .clk(CLK));  // open: clr
  Register #(.width(1), .Select("low")) VALID_5 (.D(1'b1), .en(and_6_out), .Q(VALID_5_q), .clk(CLK));  // open: clr
  Register #(.width(1), .Select("low")) VALID_6 (.D(1'b1), .en(and_7_out), .Q(VALID_6_q), .clk(CLK));  // open: clr
  Register #(.width(1), .Select("low")) VALID_7 (.D(1'b1), .en(and_8_out), .Q(VALID_7_q), .clk(CLK));  // open: clr
  Register #(.width(1), .Select("low")) VALID_8 (.D(1'b1), .en(and_9_out), .Q(VALID_8_q), .clk(CLK));  // open: clr
  Multiplexer #(.select(2), .width(8)) multiplexer_1 (
    .in0(SlotData[7:0]), .in1(SlotData[15:8]), .in2(SlotData[23:16]), .in3(SlotData[31:24]), .out(DataOut),
    .sel(Addr[1:0]), .en(Hit));
  assign Valid = L0 ? VALID_q : 1'bz;  // Controlled_Buffer controlled_buffer_1
  assign Valid = L1 ? VALID_2_q : 1'bz;  // Controlled_Buffer controlled_buffer_2
  assign Valid = L2 ? VALID_3_q : 1'bz;  // Controlled_Buffer controlled_buffer_3
  assign Valid = L3 ? VALID_4_q : 1'bz;  // Controlled_Buffer controlled_buffer_4
  assign Valid = L4 ? VALID_5_q : 1'bz;  // Controlled_Buffer controlled_buffer_5
  assign Valid = L5 ? VALID_6_q : 1'bz;  // Controlled_Buffer controlled_buffer_6
  assign Valid = L6 ? VALID_7_q : 1'bz;  // Controlled_Buffer controlled_buffer_7
  assign Valid = L7 ? VALID_8_q : 1'bz;  // Controlled_Buffer controlled_buffer_8
  assign TagData = L0 ? TAG_q : 10'bz;  // Controlled_Buffer controlled_buffer_9
  Register #(.width(10), .Select("low")) TAG (.D(Addr[15:6]), .en(and_2_out), .Q(TAG_q), .clk(CLK));  // open: clr
  assign TagData = L1 ? TAG_2_q : 10'bz;  // Controlled_Buffer controlled_buffer_10
  Register #(.width(10), .Select("low")) TAG_2 (.D(Addr[15:6]), .en(and_3_out), .Q(TAG_2_q), .clk(CLK));  // open: clr
  Register #(.width(10), .Select("low")) TAG_3 (.D(Addr[15:6]), .en(and_4_out), .Q(TAG_3_q), .clk(CLK));  // open: clr
  assign TagData = L2 ? TAG_3_q : 10'bz;  // Controlled_Buffer controlled_buffer_11
  assign TagData = L3 ? TAG_4_q : 10'bz;  // Controlled_Buffer controlled_buffer_12
  Register #(.width(10), .Select("low")) TAG_4 (.D(Addr[15:6]), .en(and_5_out), .Q(TAG_4_q), .clk(CLK));  // open: clr
  assign TagData = L4 ? TAG_5_q : 10'bz;  // Controlled_Buffer controlled_buffer_13
  Register #(.width(10), .Select("low")) TAG_5 (.D(Addr[15:6]), .en(and_6_out), .Q(TAG_5_q), .clk(CLK));  // open: clr
  assign TagData = L5 ? TAG_6_q : 10'bz;  // Controlled_Buffer controlled_buffer_14
  Register #(.width(10), .Select("low")) TAG_6 (.D(Addr[15:6]), .en(and_7_out), .Q(TAG_6_q), .clk(CLK));  // open: clr
  assign TagData = L6 ? TAG_7_q : 10'bz;  // Controlled_Buffer controlled_buffer_15
  Register #(.width(10), .Select("low")) TAG_7 (.D(Addr[15:6]), .en(and_8_out), .Q(TAG_7_q), .clk(CLK));  // open: clr
  assign TagData = L7 ? TAG_8_q : 10'bz;  // Controlled_Buffer controlled_buffer_16
  Register #(.width(10), .Select("low")) TAG_8 (.D(Addr[15:6]), .en(and_9_out), .Q(TAG_8_q), .clk(CLK));  // open: clr
  Comparator #(.width(10)) comparator_1 (.a(Addr[15:6]), .b(TagData), .eq(comparator_1_eq));  // open: gt, lt
  Decoder #(.select(4), .disabled(0), .enable("false")) decoder_1 (
    .out0(L0), .out1(L1), .out2(L2), .out3(L3), .out4(L4), .out5(L5), .out6(L6), .out7(L7), .out8(L8),
    .out9(L9), .out10(L10), .out11(L11), .out12(L12), .out13(L13), .out14(L14), .out15(L15), .sel(Addr[5:2]));
  and and_1 (Hit, comparator_1_eq, Valid);
  Register #(.width(32), .Select("low")) \u_数据块副本  (
    .D(BlockDataIn), .en(and_2_out), .Q(\数据块副本_q ), .clk(CLK));  // open: clr
  Register #(.width(32), .Select("low")) DATA_COPY (
    .D(BlockDataIn), .en(and_3_out), .Q(DATA_COPY_q), .clk(CLK));  // open: clr
  Register #(.width(32), .Select("low")) \u_数据块副本_2  (
    .D(BlockDataIn), .en(and_4_out), .Q(\数据块副本_2_q ), .clk(CLK));  // open: clr
  Register #(.width(32), .Select("low")) DATA_COPY_2 (
    .D(BlockDataIn), .en(and_5_out), .Q(DATA_COPY_2_q), .clk(CLK));  // open: clr
  Register #(.width(32), .Select("low")) \u_数据块副本_3  (
    .D(BlockDataIn), .en(and_6_out), .Q(\数据块副本_3_q ), .clk(CLK));  // open: clr
  Register #(.width(32), .Select("low")) DATA_COPY_3 (
    .D(BlockDataIn), .en(and_7_out), .Q(DATA_COPY_3_q), .clk(CLK));  // open: clr
  Register #(.width(32), .Select("low")) \u_数据块副本_4  (
    .D(BlockDataIn), .en(and_8_out), .Q(\数据块副本_4_q ), .clk(CLK));  // open: clr
  Register #(.width(32), .Select("low")) DATA_COPY_4 (
    .D(BlockDataIn), .en(and_9_out), .Q(DATA_COPY_4_q), .clk(CLK));  // open: clr
  not not_1 (Miss, Hit);
  assign SlotData = L0 ? \数据块副本_q  : 32'bz;  // Controlled_Buffer controlled_buffer_17
  assign SlotData = L1 ? DATA_COPY_q : 32'bz;  // Controlled_Buffer controlled_buffer_18
  assign SlotData = L2 ? \数据块副本_2_q  : 32'bz;  // Controlled_Buffer controlled_buffer_19
  assign SlotData = L3 ? DATA_COPY_2_q : 32'bz;  // Controlled_Buffer controlled_buffer_20
  assign SlotData = L4 ? \数据块副本_3_q  : 32'bz;  // Controlled_Buffer controlled_buffer_21
  assign SlotData = L5 ? DATA_COPY_3_q : 32'bz;  // Controlled_Buffer controlled_buffer_22
  assign SlotData = L6 ? \数据块副本_4_q  : 32'bz;  // Controlled_Buffer controlled_buffer_23
  assign SlotData = L7 ? DATA_COPY_4_q : 32'bz;  // Controlled_Buffer controlled_buffer_24
  and and_2 (and_2_out, L0, BlkDataReady);
  and and_3 (and_3_out, L1, BlkDataReady);
  and and_4 (and_4_out, L2, BlkDataReady);
  and and_5 (and_5_out, L3, BlkDataReady);
  and and_6 (and_6_out, L4, BlkDataReady);
  and and_7 (and_7_out, L5, BlkDataReady);
  and and_8 (and_8_out, L6, BlkDataReady);
  and and_9 (and_9_out, L7, BlkDataReady);
  assign Valid = L8 ? VALID_9_q : 1'bz;  // Controlled_Buffer controlled_buffer_25
  Register #(.width(1), .Select("low")) VALID_9 (.D(1'b1), .en(and_10_out), .Q(VALID_9_q), .clk(CLK));  // open: clr
  assign Valid = L9 ? VALID_10_q : 1'bz;  // Controlled_Buffer controlled_buffer_26
  Register #(.width(1), .Select("low")) VALID_10 (.D(1'b1), .en(and_11_out), .Q(VALID_10_q), .clk(CLK));  // open: clr
  Register #(.width(1), .Select("low")) VALID_11 (.D(1'b1), .en(and_12_out), .Q(VALID_11_q), .clk(CLK));  // open: clr
  assign Valid = L10 ? VALID_11_q : 1'bz;  // Controlled_Buffer controlled_buffer_27
  assign Valid = L11 ? VALID_12_q : 1'bz;  // Controlled_Buffer controlled_buffer_28
  Register #(.width(1), .Select("low")) VALID_12 (.D(1'b1), .en(and_13_out), .Q(VALID_12_q), .clk(CLK));  // open: clr
  assign Valid = L12 ? VALID_13_q : 1'bz;  // Controlled_Buffer controlled_buffer_29
  Register #(.width(1), .Select("low")) VALID_13 (.D(1'b1), .en(and_14_out), .Q(VALID_13_q), .clk(CLK));  // open: clr
  assign Valid = L13 ? VALID_14_q : 1'bz;  // Controlled_Buffer controlled_buffer_30
  Register #(.width(1), .Select("low")) VALID_14 (.D(1'b1), .en(and_15_out), .Q(VALID_14_q), .clk(CLK));  // open: clr
  assign Valid = L14 ? VALID_15_q : 1'bz;  // Controlled_Buffer controlled_buffer_31
  Register #(.width(1), .Select("low")) VALID_15 (.D(1'b1), .en(and_16_out), .Q(VALID_15_q), .clk(CLK));  // open: clr
  Register #(.width(1), .Select("low")) VALID_16 (.D(1'b1), .en(and_17_out), .Q(VALID_16_q), .clk(CLK));  // open: clr
  assign Valid = L15 ? VALID_16_q : 1'bz;  // Controlled_Buffer controlled_buffer_32
  Register #(.width(10), .Select("low")) TAG_9 (.D(Addr[15:6]), .en(and_10_out), .Q(TAG_9_q), .clk(CLK));  // open: clr
  Register #(.width(10), .Select("low")) TAG_10 (
    .D(Addr[15:6]), .en(and_11_out), .Q(TAG_10_q), .clk(CLK));  // open: clr
  Register #(.width(10), .Select("low")) TAG_11 (
    .D(Addr[15:6]), .en(and_12_out), .Q(TAG_11_q), .clk(CLK));  // open: clr
  Register #(.width(10), .Select("low")) TAG_12 (
    .D(Addr[15:6]), .en(and_13_out), .Q(TAG_12_q), .clk(CLK));  // open: clr
  Register #(.width(10), .Select("low")) TAG_13 (
    .D(Addr[15:6]), .en(and_14_out), .Q(TAG_13_q), .clk(CLK));  // open: clr
  Register #(.width(10), .Select("low")) TAG_14 (
    .D(Addr[15:6]), .en(and_15_out), .Q(TAG_14_q), .clk(CLK));  // open: clr
  Register #(.width(10), .Select("low")) TAG_15 (
    .D(Addr[15:6]), .en(and_16_out), .Q(TAG_15_q), .clk(CLK));  // open: clr
  Register #(.width(10), .Select("low")) TAG_16 (
    .D(Addr[15:6]), .en(and_17_out), .Q(TAG_16_q), .clk(CLK));  // open: clr
  assign TagData = L8 ? TAG_9_q : 10'bz;  // Controlled_Buffer controlled_buffer_33
  assign TagData = L9 ? TAG_10_q : 10'bz;  // Controlled_Buffer controlled_buffer_34
  assign TagData = L10 ? TAG_11_q : 10'bz;  // Controlled_Buffer controlled_buffer_35
  assign TagData = L11 ? TAG_12_q : 10'bz;  // Controlled_Buffer controlled_buffer_36
  assign TagData = L12 ? TAG_13_q : 10'bz;  // Controlled_Buffer controlled_buffer_37
  assign TagData = L13 ? TAG_14_q : 10'bz;  // Controlled_Buffer controlled_buffer_38
  assign TagData = L14 ? TAG_15_q : 10'bz;  // Controlled_Buffer controlled_buffer_39
  assign TagData = L15 ? TAG_16_q : 10'bz;  // Controlled_Buffer controlled_buffer_40
  assign SlotData = L8 ? \数据块副本_5_q  : 32'bz;  // Controlled_Buffer controlled_buffer_41
  Register #(.width(32), .Select("low")) \u_数据块副本_5  (
    .D(BlockDataIn), .en(and_10_out), .Q(\数据块副本_5_q ), .clk(CLK));  // open: clr
  Register #(.width(32), .Select("low")) DATA_COPY_5 (
    .D(BlockDataIn), .en(and_11_out), .Q(DATA_COPY_5_q), .clk(CLK));  // open: clr
  assign SlotData = L9 ? DATA_COPY_5_q : 32'bz;  // Controlled_Buffer controlled_buffer_42
  Register #(.width(32), .Select("low")) \u_数据块副本_6  (
    .D(BlockDataIn), .en(and_12_out), .Q(\数据块副本_6_q ), .clk(CLK));  // open: clr
  assign SlotData = L10 ? \数据块副本_6_q  : 32'bz;  // Controlled_Buffer controlled_buffer_43
  assign SlotData = L11 ? DATA_COPY_6_q : 32'bz;  // Controlled_Buffer controlled_buffer_44
  Register #(.width(32), .Select("low")) DATA_COPY_6 (
    .D(BlockDataIn), .en(and_13_out), .Q(DATA_COPY_6_q), .clk(CLK));  // open: clr
  Register #(.width(32), .Select("low")) \u_数据块副本_7  (
    .D(BlockDataIn), .en(and_14_out), .Q(\数据块副本_7_q ), .clk(CLK));  // open: clr
  assign SlotData = L12 ? \数据块副本_7_q  : 32'bz;  // Controlled_Buffer controlled_buffer_45
  assign SlotData = L13 ? DATA_COPY_7_q : 32'bz;  // Controlled_Buffer controlled_buffer_46
  Register #(.width(32), .Select("low")) DATA_COPY_7 (
    .D(BlockDataIn), .en(and_15_out), .Q(DATA_COPY_7_q), .clk(CLK));  // open: clr
  assign SlotData = L14 ? \数据块副本_8_q  : 32'bz;  // Controlled_Buffer controlled_buffer_47
  Register #(.width(32), .Select("low")) \u_数据块副本_8  (
    .D(BlockDataIn), .en(and_16_out), .Q(\数据块副本_8_q ), .clk(CLK));  // open: clr
  Register #(.width(32), .Select("low")) DATA_COPY_8 (
    .D(BlockDataIn), .en(and_17_out), .Q(DATA_COPY_8_q), .clk(CLK));  // open: clr
  assign SlotData = L15 ? DATA_COPY_8_q : 32'bz;  // Controlled_Buffer controlled_buffer_48
  and and_10 (and_10_out, L8, BlkDataReady);
  and and_11 (and_11_out, L9, BlkDataReady);
  and and_12 (and_12_out, L10, BlkDataReady);
  and and_13 (and_13_out, L11, BlkDataReady);
  and and_14 (and_14_out, L12, BlkDataReady);
  and and_15 (and_15_out, L13, BlkDataReady);
  and and_16 (and_16_out, L14, BlkDataReady);
  and and_17 (and_17_out, L15, BlkDataReady);

  // Other names for the same wires on the sheet: Blk[31:0] = BlockDataIn; BlkReady = BlkDataReady;
  //   Offset[1:0] = Addr[1:0]; 字节地址[15:0] = Addr; Index[3:0] = Addr[5:2]; Tag[9:0] = Addr[15:6]

  // Notes on the sheet:
  //   输入引脚区
  //   有效位
  //   三态门控制多行输出
  //   行选中
  //   有效位
  //   三态门控制多行输出
  //   行选中
  //   有效位
  //   三态门控制多行输出
  //   行选中
  //   有效位
  //   三态门控制多行输出
  //   行选中
  //   标记位
  //   标记位
  //   标记位
  //   标记位
  //   cache（直接相联映射）电路（16个cache块）
  //   请同学们在此设计电路！
  //   块数据输出
  //   块数据输出
  //   块数据输出
  //   块数据输出
  //   输出引脚区
  //   标记位
  //   有效位
  //   三态门控制多行输出
  //   行选中
  //   标记位
  //   有效位
  //   三态门控制多行输出
  //   行选中
  //   标记位
  //   有效位
  //   三态门控制多行输出
  //   行选中
  //   标记位
  //   有效位
  //   三态门控制多行输出
  //   行选中
  //   块数据输出
  //   块数据输出
  //   块数据输出
  //   块数据输出
endmodule

// 2路组相联cache
module \cache_2路组相联_电路_16个cache块  (
  input  BlkDataReady,
  input  [15:0] Addr,
  input  [31:0] BlockDataIn,
  input  CLK,
  output Miss,
  output [7:0] DataOut
);

  wire and_1_out, and_2_out, and_3_out, and_4_out, and_5_out, and_6_out, and_7_out, and_8_out, and_11_out,
       and_12_out, and_13_out, and_14_out, and_15_out, and_16_out, and_17_out, and_18_out, and_19_out,
       and_20_out, and_21_out, and_22_out, and_23_out, and_24_out, and_25_out, and_26_out, and_27_out,
       and_28_out, and_29_out, and_30_out, and_31_out, and_32_out, and_33_out, and_34_out, decoder_2_out0,
       decoder_2_out1, Hit, L0, L1, R0, R1, register_1_q, register_2_q, register_3_q, register_4_q,
       register_5_q, register_6_q, register_7_q, register_8_q, register_25_q, register_26_q, register_27_q,
       register_28_q, register_29_q, register_30_q, register_31_q, register_32_q, Set0, Set1, Set2, Set3,
       Set4, Set5, Set6, Set7, V0, V1;
  wire [1:0] \max2_归并比较_电路_1_p5 ;
  wire [10:0] register_9_q, register_10_q, register_11_q, register_12_q, register_13_q, register_14_q,
       register_15_q, register_16_q, register_33_q, register_34_q, register_35_q, register_36_q,
       register_37_q, register_38_q, register_39_q, register_40_q, Tag0, Tag1;
  wire [15:0] C0, C1, counter_1_q, counter_2_q, counter_3_q, counter_4_q, counter_5_q, counter_6_q,
       counter_7_q, counter_8_q, counter_9_q, counter_10_q, counter_11_q, counter_12_q, counter_13_q,
       counter_14_q, counter_15_q, counter_16_q;
  wire [31:0] register_17_q, register_18_q, register_19_q, register_20_q, register_21_q, register_22_q,
       register_23_q, register_24_q, register_41_q, register_42_q, register_43_q, register_44_q,
       register_45_q, register_46_q, register_47_q, register_48_q, SlotData;

  assign V0 = Set0 ? register_1_q : 1'bz;  // Controlled_Buffer controlled_buffer_1
  Register #(.width(1), .Select("low")) register_1 (
    .D(1'b1), .en(and_3_out), .Q(register_1_q), .clk(CLK));  // open: clr
  Register #(.width(1), .Select("low")) register_2 (
    .D(1'b1), .en(and_4_out), .Q(register_2_q), .clk(CLK));  // open: clr
  Register #(.width(1), .Select("low")) register_3 (
    .D(1'b1), .en(and_5_out), .Q(register_3_q), .clk(CLK));  // open: clr
  assign V0 = Set1 ? register_3_q : 1'bz;  // Controlled_Buffer controlled_buffer_2
  Register #(.width(1), .Select("low")) register_4 (
    .D(1'b1), .en(and_6_out), .Q(register_4_q), .clk(CLK));  // open: clr
  Register #(.width(1), .Select("low")) register_5 (
    .D(1'b1), .en(and_1_out), .Q(register_5_q), .clk(CLK));  // open: clr
  assign V0 = Set2 ? register_5_q : 1'bz;  // Controlled_Buffer controlled_buffer_3
  and and_1 (and_1_out, Set2, R0);
  Register #(.width(1), .Select("low")) register_6 (
    .D(1'b1), .en(and_7_out), .Q(register_6_q), .clk(CLK));  // open: clr
  assign V1 = Set2 ? register_6_q : 1'bz;  // Controlled_Buffer controlled_buffer_4
  assign V0 = Set3 ? register_7_q : 1'bz;  // Controlled_Buffer controlled_buffer_5
  Register #(.width(1), .Select("low")) register_7 (
    .D(1'b1), .en(and_2_out), .Q(register_7_q), .clk(CLK));  // open: clr
  and and_2 (and_2_out, Set3, R0);
  Register #(.width(1), .Select("low")) register_8 (
    .D(1'b1), .en(and_8_out), .Q(register_8_q), .clk(CLK));  // open: clr
  assign V1 = Set3 ? register_8_q : 1'bz;  // Controlled_Buffer controlled_buffer_6
  Comparator #(.width(12)) comparator_1 (.a({V0, Tag0}), .b({1'b1, Addr[15:5]}), .eq(L0));  // open: gt, lt
  Comparator #(.width(12)) comparator_2 (.a({V1, Tag1}), .b({1'b1, Addr[15:5]}), .eq(L1));  // open: gt, lt
  or or_1 (Hit, L1, L0);
  and and_3 (and_3_out, Set0, R0);
  assign V1 = Set0 ? register_2_q : 1'bz;  // Controlled_Buffer controlled_buffer_7
  and and_4 (and_4_out, Set0, R1);
  and and_5 (and_5_out, Set1, R0);
  assign V1 = Set1 ? register_4_q : 1'bz;  // Controlled_Buffer controlled_buffer_8
  and and_6 (and_6_out, Set1, R1);
  and and_7 (and_7_out, Set2, R1);
  and and_8 (and_8_out, Set3, R1);
  Decoder #(.select(3)) decoder_1 (
    .out0(Set0), .out1(Set1), .out2(Set2), .out3(Set3), .out4(Set4), .out5(Set5), .out6(Set6), .out7(Set7),
    .sel(Addr[4:2]));  // open: en
  not not_1 (Miss, Hit);
  Register #(.width(11), .Select("low")) register_9 (
    .D(Addr[15:5]), .en(and_3_out), .Q(register_9_q), .clk(CLK));  // open: clr
  Register #(.width(11), .Select("low")) register_10 (
    .D(Addr[15:5]), .en(and_4_out), .Q(register_10_q), .clk(CLK));  // open: clr
  Register #(.width(11), .Select("low")) register_11 (
    .D(Addr[15:5]), .en(and_5_out), .Q(register_11_q), .clk(CLK));  // open: clr
  Register #(.width(11), .Select("low")) register_12 (
    .D(Addr[15:5]), .en(and_6_out), .Q(register_12_q), .clk(CLK));  // open: clr
  Register #(.width(11), .Select("low")) register_13 (
    .D(Addr[15:5]), .en(and_1_out), .Q(register_13_q), .clk(CLK));  // open: clr
  assign Tag0 = Set2 ? register_13_q : 11'bz;  // Controlled_Buffer controlled_buffer_9
  Register #(.width(11), .Select("low")) register_14 (
    .D(Addr[15:5]), .en(and_7_out), .Q(register_14_q), .clk(CLK));  // open: clr
  Register #(.width(11), .Select("low")) register_15 (
    .D(Addr[15:5]), .en(and_2_out), .Q(register_15_q), .clk(CLK));  // open: clr
  assign Tag0 = Set3 ? register_15_q : 11'bz;  // Controlled_Buffer controlled_buffer_10
  Register #(.width(11), .Select("low")) register_16 (
    .D(Addr[15:5]), .en(and_8_out), .Q(register_16_q), .clk(CLK));  // open: clr
  assign Tag0 = Set0 ? register_9_q : 11'bz;  // Controlled_Buffer controlled_buffer_11
  assign Tag1 = Set0 ? register_10_q : 11'bz;  // Controlled_Buffer controlled_buffer_12
  assign Tag0 = Set1 ? register_11_q : 11'bz;  // Controlled_Buffer controlled_buffer_13
  assign Tag1 = Set1 ? register_12_q : 11'bz;  // Controlled_Buffer controlled_buffer_14
  assign Tag1 = Set2 ? register_14_q : 11'bz;  // Controlled_Buffer controlled_buffer_15
  assign Tag1 = Set3 ? register_16_q : 11'bz;  // Controlled_Buffer controlled_buffer_16
  Counter #(.width(16), .max('hffff), .behavior("old")) counter_1 (
    .count(Hit), .Q(counter_1_q), .clk(CLK), .clr(and_11_out));  // open: load, D, carry, preset
  Counter #(.width(16), .max('hffff), .behavior("old")) counter_2 (
    .count(Hit), .Q(counter_2_q), .clk(CLK), .clr(and_12_out));  // open: load, D, carry, preset
  Counter #(.width(16), .max('hffff), .behavior("old")) counter_3 (
    .count(Hit), .Q(counter_3_q), .clk(CLK), .clr(and_13_out));  // open: load, D, carry, preset
  Counter #(.width(16), .max('hffff), .behavior("old")) counter_4 (
    .count(Hit), .Q(counter_4_q), .clk(CLK), .clr(and_14_out));  // open: load, D, carry, preset
  Multiplexer #(.select(2), .width(8)) multiplexer_1 (
    .in0(SlotData[7:0]), .in1(SlotData[15:8]), .in2(SlotData[23:16]), .in3(SlotData[31:24]), .out(DataOut),
    .sel(Addr[1:0]), .en(Hit));
  assign C0 = Set0 ? counter_1_q : 16'bz;  // Controlled_Buffer controlled_buffer_17
  assign C1 = Set0 ? counter_5_q : 16'bz;  // Controlled_Buffer controlled_buffer_18
  Counter #(.width(16), .max('hffff), .behavior("old")) counter_5 (
    .count(Hit), .Q(counter_5_q), .clk(CLK), .clr(and_15_out));  // open: load, D, carry, preset
  assign C0 = Set1 ? counter_2_q : 16'bz;  // Controlled_Buffer controlled_buffer_19
  Counter #(.width(16), .max('hffff), .behavior("old")) counter_6 (
    .count(Hit), .Q(counter_6_q), .clk(CLK), .clr(and_16_out));  // open: load, D, carry, preset
  assign C1 = Set1 ? counter_6_q : 16'bz;  // Controlled_Buffer controlled_buffer_20
  assign C0 = Set2 ? counter_3_q : 16'bz;  // Controlled_Buffer controlled_buffer_21
  assign C1 = Set2 ? counter_7_q : 16'bz;  // Controlled_Buffer controlled_buffer_22
  Counter #(.width(16), .max('hffff), .behavior("old")) counter_7 (
    .count(Hit), .Q(counter_7_q), .clk(CLK), .clr(and_17_out));  // open: load, D, carry, preset
  assign C0 = Set3 ? counter_4_q : 16'bz;  // Controlled_Buffer controlled_buffer_23
  assign C1 = Set3 ? counter_8_q : 16'bz;  // Controlled_Buffer controlled_buffer_24
  Counter #(.width(16), .max('hffff), .behavior("old")) counter_8 (
    .count(Hit), .Q(counter_8_q), .clk(CLK), .clr(and_18_out));  // open: load, D, carry, preset
  and and_9 (R0, BlkDataReady, decoder_2_out0);
  and and_10 (R1, decoder_2_out1, BlkDataReady);
  // Max2_归并比较_电路 max2_归并比较_电路_1: pin names not known; wires that end beside it: C0, 2'b00, C1, 2'b01, \max2_归并比较_电路_1_p5 
  Decoder #(.select(2)) decoder_2 (
    .out0(decoder_2_out0), .out1(decoder_2_out1), .sel(\max2_归并比较_电路_1_p5 ));  // open: out2, out3, en
  assign SlotData = and_11_out ? register_17_q : 32'bz;  // Controlled_Buffer controlled_buffer_25
  Register #(.width(32), .Select("low")) register_17 (
    .D(BlockDataIn), .en(and_3_out), .Q(register_17_q), .clk(CLK));  // open: clr
  and and_11 (and_11_out, L0, Set0);
  Register #(.width(32), .Select("low")) register_18 (
    .D(BlockDataIn), .en(and_4_out), .Q(register_18_q), .clk(CLK));  // open: clr
  assign SlotData = and_12_out ? register_19_q : 32'bz;  // Controlled_Buffer controlled_buffer_26
  Register #(.width(32), .Select("low")) register_19 (
    .D(BlockDataIn), .en(and_5_out), .Q(register_19_q), .clk(CLK));  // open: clr
  and and_12 (and_12_out, L0, Set1);
  Register #(.width(32), .Select("low")) register_20 (
    .D(BlockDataIn), .en(and_6_out), .Q(register_20_q), .clk(CLK));  // open: clr
  assign SlotData = and_13_out ? register_21_q : 32'bz;  // Controlled_Buffer controlled_buffer_27
  Register #(.width(32), .Select("low")) register_21 (
    .D(BlockDataIn), .en(and_1_out), .Q(register_21_q), .clk(CLK));  // open: clr
  and and_13 (and_13_out, L0, Set2);
  Register #(.width(32), .Select("low")) register_22 (
    .D(BlockDataIn), .en(and_7_out), .Q(register_22_q), .clk(CLK));  // open: clr
  assign SlotData = and_17_out ? register_22_q : 32'bz;  // Controlled_Buffer controlled_buffer_28
  Register #(.width(32), .Select("low")) register_23 (
    .D(BlockDataIn), .en(and_2_out), .Q(register_23_q), .clk(CLK));  // open: clr
  assign SlotData = and_14_out ? register_23_q : 32'bz;  // Controlled_Buffer controlled_buffer_29
  and and_14 (and_14_out, L0, Set3);
  assign SlotData = and_18_out ? register_24_q : 32'bz;  // Controlled_Buffer controlled_buffer_30
  Register #(.width(32), .Select("low")) register_24 (
    .D(BlockDataIn), .en(and_8_out), .Q(register_24_q), .clk(CLK));  // open: clr
  assign SlotData = and_15_out ? register_18_q : 32'bz;  // Controlled_Buffer controlled_buffer_31
  and and_15 (and_15_out, L1, Set0);
  assign SlotData = and_16_out ? register_20_q : 32'bz;  // Controlled_Buffer controlled_buffer_32
  and and_16 (and_16_out, L1, Set1);
  and and_17 (and_17_out, L1, Set2);
  and and_18 (and_18_out, L1, Set3);
  Register #(.width(1), .Select("low")) register_25 (
    .D(1'b1), .en(and_21_out), .Q(register_25_q), .clk(CLK));  // open: clr
  Register #(.width(1), .Select("low")) register_26 (
    .D(1'b1), .en(and_23_out), .Q(register_26_q), .clk(CLK));  // open: clr
  assign V0 = Set4 ? register_27_q : 1'bz;  // Controlled_Buffer controlled_buffer_33
  Register #(.width(1), .Select("low")) register_27 (
    .D(1'b1), .en(and_19_out), .Q(register_27_q), .clk(CLK));  // open: clr
  and and_19 (and_19_out, Set4, R0);
  assign V1 = Set4 ? register_28_q : 1'bz;  // Controlled_Buffer controlled_buffer_34
  Register #(.width(1), .Select("low")) register_28 (
    .D(1'b1), .en(and_25_out), .Q(register_28_q), .clk(CLK));  // open: clr
  assign V0 = Set5 ? register_29_q : 1'bz;  // Controlled_Buffer controlled_buffer_35
  Register #(.width(1), .Select("low")) register_29 (
    .D(1'b1), .en(and_20_out), .Q(register_29_q), .clk(CLK));  // open: clr
  and and_20 (and_20_out, Set5, R0);
  Register #(.width(1), .Select("low")) register_30 (
    .D(1'b1), .en(and_26_out), .Q(register_30_q), .clk(CLK));  // open: clr
  assign V1 = Set5 ? register_30_q : 1'bz;  // Controlled_Buffer controlled_buffer_36
  assign V0 = Set6 ? register_25_q : 1'bz;  // Controlled_Buffer controlled_buffer_37
  and and_21 (and_21_out, Set6, R0);
  Register #(.width(1), .Select("low")) register_31 (
    .D(1'b1), .en(and_22_out), .Q(register_31_q), .clk(CLK));  // open: clr
  assign V1 = Set6 ? register_31_q : 1'bz;  // Controlled_Buffer controlled_buffer_38
  and and_22 (and_22_out, Set6, R1);
  assign V0 = Set7 ? register_26_q : 1'bz;  // Controlled_Buffer controlled_buffer_39
  and and_23 (and_23_out, Set7, R0);
  Register #(.width(1), .Select("low")) register_32 (
    .D(1'b1), .en(and_24_out), .Q(register_32_q), .clk(CLK));  // open: clr
  assign V1 = Set7 ? register_32_q : 1'bz;  // Controlled_Buffer controlled_buffer_40
  and and_24 (and_24_out, Set7, R1);
  and and_25 (and_25_out, Set4, R1);
  and and_26 (and_26_out, Set5, R1);
  Register #(.width(11), .Select("low")) register_33 (
    .D(Addr[15:5]), .en(and_19_out), .Q(register_33_q), .clk(CLK));  // open: clr
  assign Tag0 = Set4 ? register_33_q : 11'bz;  // Controlled_Buffer controlled_buffer_41
  Register #(.width(11), .Select("low")) register_34 (
    .D(Addr[15:5]), .en(and_25_out), .Q(register_34_q), .clk(CLK));  // open: clr
  Register #(.width(11), .Select("low")) register_35 (
    .D(Addr[15:5]), .en(and_20_out), .Q(register_35_q), .clk(CLK));  // open: clr
  assign Tag0 = Set5 ? register_35_q : 11'bz;  // Controlled_Buffer controlled_buffer_42
  Register #(.width(11), .Select("low")) register_36 (
    .D(Addr[15:5]), .en(and_26_out), .Q(register_36_q), .clk(CLK));  // open: clr
  assign Tag0 = Set6 ? register_37_q : 11'bz;  // Controlled_Buffer controlled_buffer_43
  Register #(.width(11), .Select("low")) register_37 (
    .D(Addr[15:5]), .en(and_21_out), .Q(register_37_q), .clk(CLK));  // open: clr
  assign Tag1 = Set6 ? register_38_q : 11'bz;  // Controlled_Buffer controlled_buffer_44
  Register #(.width(11), .Select("low")) register_38 (
    .D(Addr[15:5]), .en(and_22_out), .Q(register_38_q), .clk(CLK));  // open: clr
  assign Tag0 = Set7 ? register_39_q : 11'bz;  // Controlled_Buffer controlled_buffer_45
  Register #(.width(11), .Select("low")) register_39 (
    .D(Addr[15:5]), .en(and_23_out), .Q(register_39_q), .clk(CLK));  // open: clr
  assign Tag1 = Set7 ? register_40_q : 11'bz;  // Controlled_Buffer controlled_buffer_46
  Register #(.width(11), .Select("low")) register_40 (
    .D(Addr[15:5]), .en(and_24_out), .Q(register_40_q), .clk(CLK));  // open: clr
  assign Tag1 = Set4 ? register_34_q : 11'bz;  // Controlled_Buffer controlled_buffer_47
  assign Tag1 = Set5 ? register_36_q : 11'bz;  // Controlled_Buffer controlled_buffer_48
  Counter #(.width(16), .max('hffff), .behavior("old")) counter_9 (
    .count(Hit), .Q(counter_9_q), .clk(CLK), .clr(and_27_out));  // open: load, D, carry, preset
  Counter #(.width(16), .max('hffff), .behavior("old")) counter_10 (
    .count(Hit), .Q(counter_10_q), .clk(CLK), .clr(and_28_out));  // open: load, D, carry, preset
  Counter #(.width(16), .max('hffff), .behavior("old")) counter_11 (
    .count(Hit), .Q(counter_11_q), .clk(CLK), .clr(and_29_out));  // open: load, D, carry, preset
  Counter #(.width(16), .max('hffff), .behavior("old")) counter_12 (
    .count(Hit), .Q(counter_12_q), .clk(CLK), .clr(and_30_out));  // open: load, D, carry, preset
  Counter #(.width(16), .max('hffff), .behavior("old")) counter_13 (
    .count(Hit), .Q(counter_13_q), .clk(CLK), .clr(and_31_out));  // open: load, D, carry, preset
  Counter #(.width(16), .max('hffff), .behavior("old")) counter_14 (
    .count(Hit), .Q(counter_14_q), .clk(CLK), .clr(and_32_out));  // open: load, D, carry, preset
  Counter #(.width(16), .max('hffff), .behavior("old")) counter_15 (
    .count(Hit), .Q(counter_15_q), .clk(CLK), .clr(and_33_out));  // open: load, D, carry, preset
  Counter #(.width(16), .max('hffff), .behavior("old")) counter_16 (
    .count(Hit), .Q(counter_16_q), .clk(CLK), .clr(and_34_out));  // open: load, D, carry, preset
  assign C0 = Set4 ? counter_9_q : 16'bz;  // Controlled_Buffer controlled_buffer_49
  assign C1 = Set4 ? counter_10_q : 16'bz;  // Controlled_Buffer controlled_buffer_50
  assign C0 = Set5 ? counter_11_q : 16'bz;  // Controlled_Buffer controlled_buffer_51
  assign C1 = Set5 ? counter_12_q : 16'bz;  // Controlled_Buffer controlled_buffer_52
  assign C0 = Set6 ? counter_13_q : 16'bz;  // Controlled_Buffer controlled_buffer_53
  assign C1 = Set6 ? counter_14_q : 16'bz;  // Controlled_Buffer controlled_buffer_54
  assign C0 = Set7 ? counter_15_q : 16'bz;  // Controlled_Buffer controlled_buffer_55
  assign C1 = Set7 ? counter_16_q : 16'bz;  // Controlled_Buffer controlled_buffer_56
  Register #(.width(32), .Select("low")) register_41 (
    .D(BlockDataIn), .en(and_21_out), .Q(register_41_q), .clk(CLK));  // open: clr
  Register #(.width(32), .Select("low")) register_42 (
    .D(BlockDataIn), .en(and_23_out), .Q(register_42_q), .clk(CLK));  // open: clr
  assign SlotData = and_27_out ? register_43_q : 32'bz;  // Controlled_Buffer controlled_buffer_57
  Register #(.width(32), .Select("low")) register_43 (
    .D(BlockDataIn), .en(and_19_out), .Q(register_43_q), .clk(CLK));  // open: clr
  and and_27 (and_27_out, L0, Set4);
  assign SlotData = and_28_out ? register_44_q : 32'bz;  // Controlled_Buffer controlled_buffer_58
  Register #(.width(32), .Select("low")) register_44 (
    .D(BlockDataIn), .en(and_25_out), .Q(register_44_q), .clk(CLK));  // open: clr
  and and_28 (and_28_out, L1, Set4);
  assign SlotData = and_29_out ? register_45_q : 32'bz;  // Controlled_Buffer controlled_buffer_59
  Register #(.width(32), .Select("low")) register_45 (
    .D(BlockDataIn), .en(and_20_out), .Q(register_45_q), .clk(CLK));  // open: clr
  and and_29 (and_29_out, L0, Set5);
  assign SlotData = and_30_out ? register_46_q : 32'bz;  // Controlled_Buffer controlled_buffer_60
  Register #(.width(32), .Select("low")) register_46 (
    .D(BlockDataIn), .en(and_26_out), .Q(register_46_q), .clk(CLK));  // open: clr
  and and_30 (and_30_out, L1, Set5);
  assign SlotData = and_31_out ? register_41_q : 32'bz;  // Controlled_Buffer controlled_buffer_61
  and and_31 (and_31_out, L0, Set6);
  assign SlotData = and_32_out ? register_47_q : 32'bz;  // Controlled_Buffer controlled_buffer_62
  Register #(.width(32), .Select("low")) register_47 (
    .D(BlockDataIn), .en(and_22_out), .Q(register_47_q), .clk(CLK));  // open: clr
  and and_32 (and_32_out, L1, Set6);
  assign SlotData = and_33_out ? register_42_q : 32'bz;  // Controlled_Buffer controlled_buffer_63
  and and_33 (and_33_out, L0, Set7);
  Register #(.width(32), .Select("low")) register_48 (
    .D(BlockDataIn), .en(and_24_out), .Q(register_48_q), .clk(CLK));  // open: clr
  assign SlotData = and_34_out ? register_48_q : 32'bz;  // Controlled_Buffer controlled_buffer_64
  and and_34 (and_34_out, L1, Set7);

  // Other names for the same wires on the sheet: Tag[10:0] = Addr[15:5]; 字节地址[15:0] = Addr; Blk[31:0] = BlockDataIn;
  //   BlkReady = BlkDataReady

  // Notes on the sheet:
  //   16位
  //   输入引脚区
  //   Index
  //   Offset
  //   cache（2路组相联映射）电路（16个cache块）
  //   请同学们在此设计电路！
  //   输出引脚区
endmodule

module \cache_2路组相联_测试电路_16个cache块  (
  input  in_1,
  output [3:0] Set,
  output [1:0] L,
  output [1:0] R
);

  wire and_2_out, Clk, comparator_1_lt, comparator_2_eq, comparator_3_eq, controlled_buffer_1_out, EN, Error,
       Go, Hit, Miss, or_1_out, RDY, Runing;
  wire [3:0] _1, _2, _3;
  wire [7:0] \cache块交换逻辑电路_1_p10 , Dataout;
  wire [9:0] \测试用例数 ;
  wire [15:0] adder_1_out, Addr, bit_extender_3_out, \cache块交换逻辑电路_1_p9 , counter_1_q, subtractor_1_out,
       \命中次数 , \时钟周期数 , \校验和 , \缺失次数 , \访问次数 ;
  wire [31:0] bit_extender_1_out, bit_extender_2_out, BlkDataIn, divider_1_out, divider_2_out,
       multiplier_1_out;
  wire [31:4] divider_2_rem, divider_3_out, divider_3_rem;

  not not_1 (Hit, Miss);
  and and_1 (EN, Hit, Go);
  Clock clock_1 (.out(Clk));
  Counter #(.width(16), .max('hffff), .behavior("old")) counter_1 (
    .count(and_2_out), .Q(counter_1_q), .clk(Clk));  // open: load, D, carry, clr, preset
  and and_2 (and_2_out, Miss, RDY, Runing);
  Subtractor #(.width(16)) subtractor_1 (.a(\访问次数 ), .b(\缺失次数 ), .out(subtractor_1_out));  // open: bin, bout
  Comparator #(.width(16)) comparator_1 (.a(\访问次数 ), .b(\缺失次数 ), .lt(comparator_1_lt));  // open: gt, eq
  // Probe on \访问次数 
  // Probe on \测试用例数 
  Counter #(.width(10), .max('h3ff), .behavior("old")) \u_计数器  (
    .count(EN), .Q(\测试用例数 ), .clk(Clk));  // open: load, D, carry, clr, preset
  Register #(.width(16), .Select("low")) register_1 (.D(counter_1_q), .en(EN), .Q(\缺失次数 ), .clk(Clk));  // open: clr
  Comparator #(.width(10)) comparator_2 (.a(\测试用例数 ), .b(10'h100), .eq(comparator_2_eq));  // open: gt, lt
  not not_2 (Runing, comparator_2_eq);
  Multiplexer #(.width(16), .disabled(0), .enable("false")) multiplexer_1 (
    .in0(subtractor_1_out), .in1({16{1'b0}}), .out(\命中次数 ), .sel(comparator_1_lt));
  // Probe on \命中次数 
  // Probe on \时钟周期数 
  ROM #(.addrWidth(10), .dataWidth(16), .Select("high")) \u_主存地址  (.addr(\测试用例数 ), .data(Addr));
  Counter #(.width(16), .max('hffff), .behavior("old")) counter_2 (
    .count(EN), .Q(\访问次数 ), .clk(Clk));  // open: load, D, carry, clr, preset
  assign bit_extender_1_out = {{16{1'b0}}, \命中次数 };  // Bit_Extender bit_extender_1
  // Probe on Dataout
  Multiplier #(.width(32)) multiplier_1 (
    .a(bit_extender_1_out), .b(32'h64), .out(multiplier_1_out));  // open: cin, cout
  assign bit_extender_2_out = {{16{1'b0}}, \访问次数 };  // Bit_Extender bit_extender_2
  // Probe on \缺失次数 
  // Probe on \校验和 
  \cache_2路组相联_电路_16个cache块  \cache_2路组相联_电路_16个cache块_1  (
    .BlkDataReady(RDY), .Addr(Addr), .BlockDataIn(BlkDataIn), .CLK(Clk), .Miss(Miss), .DataOut(Dataout));
  assign bit_extender_3_out = {{8{1'b0}}, Dataout};  // Bit_Extender bit_extender_3
  Divider #(.width(32)) divider_1 (
    .a(multiplier_1_out), .b(bit_extender_2_out), .out(divider_1_out));  // open: upper, rem
  Adder #(.width(16)) adder_1 (.a(\校验和 ), .b(bit_extender_3_out), .out(adder_1_out));  // open: cin, cout
  LED \u_读数据出错  (.in(Error));
  LED \u_缺失  (.in(Miss));
  Pull_Resistor #(.pull(1)) pull_resistor_1 (.node(Miss));
  Register #(.width(16), .Select("low")) \u_校验和  (.D(adder_1_out), .en(EN), .Q(\校验和 ), .clk(Clk));  // open: clr
  Divider #(.width(32)) divider_2 (
    .a(divider_1_out), .b(32'ha), .out(divider_2_out), .rem({divider_2_rem, _1}));  // open: upper
  // cache块交换逻辑电路 cache块交换逻辑电路_1: pin names not known; wires that end beside it: L, R, Miss, BlkDataIn, RDY, Addr, Runing, Clk, \cache块交换逻辑电路_1_p9 , \cache块交换逻辑电路_1_p10 
  // Probe on \校验和 
  Divider #(.width(32)) divider_3 (
    .a(divider_2_out), .b(32'ha), .out({divider_3_out, _3}), .rem({divider_3_rem, _2}));  // open: upper
  ROM #(.addrWidth(16), .Select("high")) \u_主存内容  (.addr(\cache块交换逻辑电路_1_p9 ), .data(\cache块交换逻辑电路_1_p10 ));
  Comparator comparator_3 (.a(Addr[7:0]), .b(Dataout), .eq(comparator_3_eq));  // open: gt, lt
  assign controlled_buffer_1_out = Hit ? comparator_3_eq : 1'bz;  // Controlled_Buffer controlled_buffer_1
  Pull_Resistor #(.pull(1)) pull_resistor_2 (.node(controlled_buffer_1_out));
  Hex_Digit_Display hex_digit_display_1 (.value(_2));  // open: dp
  Hex_Digit_Display hex_digit_display_2 (.value(_3), .dp(1'b1));
  or or_1 (or_1_out, controlled_buffer_1_out, ~in_1);  // OR_Gate
  Counter #(.width(16), .max('hffff), .behavior("old")) counter_3 (
    .count(Runing), .Q(\时钟周期数 ), .clk(Clk));  // open: load, D, carry, clr, preset
  Hex_Digit_Display hex_digit_display_3 (.value(_1));  // open: dp
  // Probe on Addr
  LED led_1 (.in(RDY));
  // Probe on BlkDataIn
  // Probe on Dataout
  and and_3 (Go, Runing, or_1_out);
  not not_3 (Error, or_1_out);

  // Other names for the same wires on the sheet: 读错误暂停 = in_1

  // Notes on the sheet:
  //   contents of 主存地址 (hex, n*v repeats v):
  //   0 1 2 3 8 9 a b 10 11 12 13 20 21 22 23 8 9 a b 4 5 6 7 24 25 26 27 4 5 6 7 0 1 2 3 8 9 a b 8 9 a b
  //   20 21 22 23 28 29 2a 2b 24 25 26 27 4 5 6 7 24 25 26 27 0 1 2 3 8 9 a b 20 21 22 23 20 21 22 23 30
  //   31 32 33 4 5 6 7 24 25 26 27 4 5 6 7 0 1 2 3 8 9 a b 20 21 22 23 20 21 22 23 28 29 2a 2b 4 5 6 7 24
  //   25 26 27 24 25 26 27 0 1 2 3 8 9 a b 8 9 a b 20 21 22 23 30 31 32 33 4 5 6 7 24 25 26 27 24 25 26 27
  //   0 1 2 3 0 1 2 3 8 9 a b 20 21 22 23 28 29 2a 2b 4 5 6 7 24 25 26 27 4 5 6 7 0 1 2 3 8 9 a b 0 1 2 3
  //   20 21 22 23 30 31 32 33 24 25 26 27 4 5 6 7 24 25 26 27 0 1 2 3 8 9 a b 20 21 22 23 20 21 22 23 28
  //   29 2a 2b 4 5 6 7 24 25 26 27 4 5 6 7
  //   2路组相联映射cache测试电路
  //   命中率
  //   contents of 主存内容 (hex, n*v repeats v):
  //   0 1 2 3 4 5 6 7 8 9 a b c d e f 10 11 12 13 14 15 16 17 18 19 1a 1b 1c 1d 1e 1f 20 21 22 23 24 25 26
  //   27 28 29 2a 2b 2c 2d 2e 2f 30 31 32 33 34 35 36 37 38 39 3a 3b 3c 3d 3e 3f 40 41 42 43 44 45 46 47
  //   48 49 4a 4b 4c 4d 4e 4f 50 51 52 53 54 55 56 57 58 59 5a 5b 5c 5d 5e 5f 60 61 62 63 64 65 66 67 68
  //   69 6a 6b 6c 6d 6e 6f 70 71 72 73 74 75 76 77 78 79 7a 7b 7c 7d 7e 7f 80 81 82 83 84 85 86 87 88 89
  //   8a 8b 8c 8d 8e 8f 90 91 92 93 94 95 96 97 98 99 9a 9b 9c 9d 9e 9f a0 a1 a2 a3 a4 a5 a6 a7 a8 a9 aa
  //   ab ac ad ae af b0 b1 b2 b3 b4 b5 b6 b7 b8 b9 ba bb bc bd be bf c0 c1 c2 c3 c4 c5 c6 c7 c8 c9 ca cb
  //   cc cd ce cf d0 d1 d2 d3 d4 d5 d6 d7 d8 d9 da db dc dd de df e0 e1 e2 e3 e4 e5 e6 e7 e8 e9 ea eb ec
  //   ed ee ef f0 f1 f2 f3 f4 f5 f6 f7 f8 f9 fa fb fc fd fe ff 0 1 2 3 4 5 6 7 8 9 a b c d e f 10 11 12 13
  //   14 15 16 17 18 19 1a 1b 1c 1d 1e 1f 20 21 22 23 24 25 26 27 28 29 2a 2b 2c 2d 2e 2f 30 31 32 33 34
  //   35 36 37 38 39 3a 3b 3c 3d 3e 3f 40 41 42 43 44 45 46 47 48 49 4a 4b 4c 4d 4e 4f 50 51 52 53 54 55
  //   56 57 58 59 5a 5b 5c 5d 5e 5f 60 61 62 63 64 65 66 67 68 69 6a 6b 6c 6d 6e 6f 70 71 72 73 74 75 76
  //   77 78 79 7a 7b 7c 7d 7e 7f 80 81 82 83 84 85 86 87 88 89 8a 8b 8c 8d 8e 8f 90 91 92 93 94 95 96 97
  //   98 99 9a 9b 9c 9d 9e 9f a0 a1 a2 a3 a4 a5 a6 a7 a8 a9 aa ab ac ad ae af b0 b1 b2 b3 b4 b5 b6 b7 b8
  //   b9 ba bb bc bd be bf c0 c1 c2 c3 c4 c5 c6 c7 c8 c9 ca cb cc cd ce cf d0 d1 d2 d3 d4 d5 d6 d7 d8 d9
  //   da db dc dd de df e0 e1 e2 e3 e4 e5 e6 e7 e8 e9 ea eb ec ed ee ef f0 f1 f2 f3 f4 f5 f6 f7 f8 f9 fa
  //   fb fc fd fe ff 0 1 2 3 4 5 6 7 8 9 a b c d e f 10 11 12 13 14 15 16 17 18 19 1a 1b 1c 1d 1e 1f 20 21
  //   22 23 24 25 26 27 28 29 2a 2b 2c 2d 2e 2f 30 31 32 33 34 35 36 37 38 39 3a 3b 3c 3d 3e 3f 40 41 42
  //   43 44 45 46 47 48 49 4a 4b 4c 4d 4e 4f 50 51 52 53 54 55 56 57 58 59 5a 5b 5c 5d 5e 5f 60 61 62 63
  //   64 65 66 67 68 69 6a 6b 6c 6d 6e 6f 70 71 72 73 74 75 76 77 78 79 7a 7b 7c 7d 7e 7f 80 81 82 83 84
  //   85 86 87 88 89 8a 8b 8c 8d 8e 8f 90 91 92 93 94 95 96 97 98 99 9a 9b 9c 9d 9e 9f a0 a1 a2 a3 a4 a5
  //   a6 a7 a8 a9 aa ab ac ad ae af b0 b1 b2 b3 b4 b5 b6 b7 b8 b9 ba bb bc bd be bf c0 c1 c2 c3 c4 c5 c6
  //   c7 c8 c9 ca cb cc cd ce cf d0 d1 d2 d3 d4 d5 d6 d7 d8 d9 da db dc dd de df e0 e1 e2 e3 e4 e5 e6 e7
  //   e8 e9 ea eb ec ed ee ef f0 f1 f2 f3 f4 f5 f6 f7 f8 f9 fa fb fc fd fe ff 0 1 2 3 4 5 6 7 8 9 a b c d
  //   e f 10 11 12 13 14 15 16 17 18 19 1a 1b 1c 1d 1e 1f 20 21 22 23 24 25 26 27 28 29 2a 2b 2c 2d 2e 2f
  //   30 31 32 33 34 35 36 37 38 39 3a 3b 3c 3d 3e 3f 40 41 42 43 44 45 46 47 48 49 4a 4b 4c 4d 4e 4f 50
  //   51 52 53 54 55 56 57 58 59 5a 5b 5c 5d 5e 5f 60 61 62 63 64 65 66 67 68 69 6a 6b 6c 6d 6e 6f 70 71
  //   72 73 74 75 76 77 78 79 7a 7b 7c 7d 7e 7f 80 81 82 83 84 85 86 87 88 89 8a 8b 8c 8d 8e 8f 90 91 92
  //   93 94 95 96 97 98 99 9a 9b 9c 9d 9e 9f a0 a1 a2 a3 a4 a5 a6 a7 a8 a9 aa ab ac ad ae af b0 b1 b2 b3
  //   b4 b5 b6 b7 b8 b9 ba bb bc bd be bf c0 c1 c2 c3 c4 c5 c6 c7 c8 c9 ca cb cc cd ce cf d0 d1 d2 d3 d4
  //   d5 d6 d7 d8 d9 da db dc dd de df e0 e1 e2 e3 e4 e5 e6 e7 e8 e9 ea eb ec ed ee ef f0 f1 f2 f3 f4 f5
  //   f6 f7 f8 f9 fa fb fc fd fe ff 0 1 2 3 4 5 6 7 8 9 a b c d e f 10 11 12 13 14 15 16 17 18 19 1a 1b 1c
  //   1d 1e 1f 20 21 22 23 24 25 26 27 28 29 2a 2b 2c 2d 2e 2f 30 31 32 33 34 35 36 37 38 39 3a 3b 3c 3d
  //   3e 3f 40 41 42 43 44 45 46 47 48 49 4a 4b 4c 4d 4e 4f 50 51 52 53 54 55 56 57 58 59 5a 5b 5c 5d 5e
  //   5f 60 61 62 63 64 65 66 67 68 69 6a 6b 6c 6d 6e 6f 70 71 72 73 74 75 76 77 78 79 7a 7b 7c 7d 7e 7f
  //   80 81 82 83 84 85 86 87 88 89 8a 8b 8c 8d 8e 8f 90 91 92 93 94 95 96 97 98 99 9a 9b 9c 9d 9e 9f a0
  //   a1 a2 a3 a4 a5 a6 a7 a8 a9 aa ab ac ad ae af b0 b1 b2 b3 b4 b5 b6 b7 b8 b9 ba bb bc bd be bf c0 c1
  //   c2 c3 c4 c5 c6 c7 c8 c9 ca cb cc cd ce cf d0 d1 d2 d3 d4 d5 d6 d7 d8 d9 da db dc dd de df e0 e1 e2
  //   e3 e4 e5 e6 e7 e8 e9 ea eb ec ed ee ef f0 f1 f2 f3 f4 f5 f6 f7 f8 f9 fa fb fc fd fe ff
  //   cache模拟器
endmodule

module \cache_直接相联映射_测试电路_16个cache块  (
  input  in_1,
  output [7:0] L
);

  wire and_2_out, Clk, comparator_1_lt, comparator_2_eq, comparator_3_eq, controlled_buffer_1_out, EN, Error,
       Go, Hit, Miss, or_1_out, RDY, Runing;
  wire [3:0] _1, _2, _3;
  wire [7:0] \cache块交换逻辑电路_1_p8 , Dataout;
  wire [9:0] \测试用例数 ;
  wire [15:0] adder_1_out, Addr, bit_extender_3_out, \cache块交换逻辑电路_1_p7 , counter_1_q, subtractor_1_out,
       \命中次数 , \时钟周期数 , \校验和 , \缺失次数 , \访问次数 ;
  wire [31:0] bit_extender_1_out, bit_extender_2_out, BlkDataIn, divider_1_out, divider_2_out,
       multiplier_1_out;
  wire [31:4] divider_2_rem, divider_3_out, divider_3_rem;

  not not_1 (Hit, Miss);
  and and_1 (EN, Hit, Go);
  Clock clock_1 (.out(Clk));
  Counter #(.width(16), .max('hffff), .behavior("old")) counter_1 (
    .count(and_2_out), .Q(counter_1_q), .clk(Clk));  // open: load, D, carry, clr, preset
  and and_2 (and_2_out, Miss, RDY, Runing);
  Subtractor #(.width(16)) subtractor_1 (.a(\访问次数 ), .b(\缺失次数 ), .out(subtractor_1_out));  // open: bin, bout
  Comparator #(.width(16)) comparator_1 (.a(\访问次数 ), .b(\缺失次数 ), .lt(comparator_1_lt));  // open: gt, eq
  // Probe on \访问次数 
  // Probe on \测试用例数 
  Counter #(.width(10), .max('h3ff), .behavior("old")) \u_计数器  (
    .count(EN), .Q(\测试用例数 ), .clk(Clk));  // open: load, D, carry, clr, preset
  Register #(.width(16), .Select("low")) register_1 (.D(counter_1_q), .en(EN), .Q(\缺失次数 ), .clk(Clk));  // open: clr
  not not_2 (Runing, comparator_2_eq);
  Comparator #(.width(10)) comparator_2 (.a(\测试用例数 ), .b(10'h100), .eq(comparator_2_eq));  // open: gt, lt
  Multiplexer #(.width(16), .disabled(0), .enable("false")) multiplexer_1 (
    .in0(subtractor_1_out), .in1({16{1'b0}}), .out(\命中次数 ), .sel(comparator_1_lt));
  // Probe on \命中次数 
  // Probe on \时钟周期数 
  ROM #(.addrWidth(10), .dataWidth(16), .Select("high")) \u_主存地址  (.addr(\测试用例数 ), .data(Addr));
  Counter #(.width(16), .max('hffff), .behavior("old")) counter_2 (
    .count(EN), .Q(\访问次数 ), .clk(Clk));  // open: load, D, carry, clr, preset
  assign bit_extender_1_out = {{16{1'b0}}, \命中次数 };  // Bit_Extender bit_extender_1
  // Probe on Dataout
  Multiplier #(.width(32)) multiplier_1 (
    .a(bit_extender_1_out), .b(32'h64), .out(multiplier_1_out));  // open: cin, cout
  assign bit_extender_2_out = {{16{1'b0}}, \访问次数 };  // Bit_Extender bit_extender_2
  // Probe on \缺失次数 
  // Probe on \校验和 
  \cache_直接相联映射_电路_16个cache块  \cache_直接相联映射_电路_16个cache块_1  (
    .Addr(Addr), .BlockDataIn(BlkDataIn), .BlkDataReady(RDY), .CLK(Clk), .Miss(Miss), .DataOut(Dataout));
  assign bit_extender_3_out = {{8{1'b0}}, Dataout};  // Bit_Extender bit_extender_3
  Divider #(.width(32)) divider_1 (
    .a(multiplier_1_out), .b(bit_extender_2_out), .out(divider_1_out));  // open: upper, rem
  Adder #(.width(16)) adder_1 (.a(\校验和 ), .b(bit_extender_3_out), .out(adder_1_out));  // open: cin, cout
  LED \u_读数据出错  (.in(Error));
  LED \u_缺失  (.in(Miss));
  Pull_Resistor #(.pull(1)) pull_resistor_1 (.node(Miss));
  Register #(.width(16), .Select("low")) \u_校验和  (.D(adder_1_out), .en(EN), .Q(\校验和 ), .clk(Clk));  // open: clr
  Divider #(.width(32)) divider_2 (
    .a(divider_1_out), .b(32'ha), .out(divider_2_out), .rem({divider_2_rem, _1}));  // open: upper
  // cache块交换逻辑电路 cache块交换逻辑电路_1: pin names not known; wires that end beside it: Miss, BlkDataIn, RDY, Addr, Runing, Clk, \cache块交换逻辑电路_1_p7 , \cache块交换逻辑电路_1_p8 
  // Probe on \校验和 
  Divider #(.width(32)) divider_3 (
    .a(divider_2_out), .b(32'ha), .out({divider_3_out, _3}), .rem({divider_3_rem, _2}));  // open: upper
  ROM #(.addrWidth(16), .Select("high")) \u_主存内容  (.addr(\cache块交换逻辑电路_1_p7 ), .data(\cache块交换逻辑电路_1_p8 ));
  Comparator comparator_3 (.a(Addr[7:0]), .b(Dataout), .eq(comparator_3_eq));  // open: gt, lt
  assign controlled_buffer_1_out = Hit ? comparator_3_eq : 1'bz;  // Controlled_Buffer controlled_buffer_1
  Pull_Resistor #(.pull(1)) pull_resistor_2 (.node(controlled_buffer_1_out));
  Hex_Digit_Display hex_digit_display_1 (.value(_3), .dp(1'b1));
  Hex_Digit_Display hex_digit_display_2 (.value(_2));  // open: dp
  or or_1 (or_1_out, controlled_buffer_1_out, ~in_1);  // OR_Gate
  Counter #(.width(16), .max('hffff), .behavior("old")) counter_3 (
    .count(Runing), .Q(\时钟周期数 ), .clk(Clk));  // open: load, D, carry, clr, preset
  Hex_Digit_Display hex_digit_display_3 (.value(_1));  // open: dp
  // Probe on Addr
  LED led_1 (.in(RDY));
  // Probe on BlkDataIn
  // Probe on Dataout
  and and_3 (Go, Runing, or_1_out);
  not not_3 (Error, or_1_out);

  // Other names for the same wires on the sheet: 读错误暂停 = in_1

  // Notes on the sheet:
  //   contents of 主存地址 (hex, n*v repeats v):
  //   0 1 2 3 8 9 a b 10 11 12 13 20 21 22 23 8 9 a b 4 5 6 7 24 25 26 27 4 5 6 7 0 1 2 3 8 9 a b 8 9 a b
  //   20 21 22 23 28 29 2a 2b 24 25 26 27 4 5 6 7 24 25 26 27 0 1 2 3 8 9 a b 20 21 22 23 20 21 22 23 30
  //   31 32 33 4 5 6 7 24 25 26 27 4 5 6 7 0 1 2 3 8 9 a b 20 21 22 23 20 21 22 23 28 29 2a 2b 4 5 6 7 24
  //   25 26 27 24 25 26 27 0 1 2 3 8 9 a b 8 9 a b 20 21 22 23 30 31 32 33 4 5 6 7 24 25 26 27 24 25 26 27
  //   0 1 2 3 0 1 2 3 8 9 a b 20 21 22 23 28 29 2a 2b 4 5 6 7 24 25 26 27 4 5 6 7 0 1 2 3 8 9 a b 0 1 2 3
  //   20 21 22 23 30 31 32 33 24 25 26 27 4 5 6 7 24 25 26 27 0 1 2 3 8 9 a b 20 21 22 23 20 21 22 23 28
  //   29 2a 2b 4 5 6 7 24 25 26 27 4 5 6 7
  //   直接相联映射cache测试电路
  //   命中率
  //   contents of 主存内容 (hex, n*v repeats v):
  //   0 1 2 3 4 5 6 7 8 9 a b c d e f 10 11 12 13 14 15 16 17 18 19 1a 1b 1c 1d 1e 1f 20 21 22 23 24 25 26
  //   27 28 29 2a 2b 2c 2d 2e 2f 30 31 32 33 34 35 36 37 38 39 3a 3b 3c 3d 3e 3f 40 41 42 43 44 45 46 47
  //   48 49 4a 4b 4c 4d 4e 4f 50 51 52 53 54 55 56 57 58 59 5a 5b 5c 5d 5e 5f 60 61 62 63 64 65 66 67 68
  //   69 6a 6b 6c 6d 6e 6f 70 71 72 73 74 75 76 77 78 79 7a 7b 7c 7d 7e 7f 80 81 82 83 84 85 86 87 88 89
  //   8a 8b 8c 8d 8e 8f 90 91 92 93 94 95 96 97 98 99 9a 9b 9c 9d 9e 9f a0 a1 a2 a3 a4 a5 a6 a7 a8 a9 aa
  //   ab ac ad ae af b0 b1 b2 b3 b4 b5 b6 b7 b8 b9 ba bb bc bd be bf c0 c1 c2 c3 c4 c5 c6 c7 c8 c9 ca cb
  //   cc cd ce cf d0 d1 d2 d3 d4 d5 d6 d7 d8 d9 da db dc dd de df e0 e1 e2 e3 e4 e5 e6 e7 e8 e9 ea eb ec
  //   ed ee ef f0 f1 f2 f3 f4 f5 f6 f7 f8 f9 fa fb fc fd fe ff 0 1 2 3 4 5 6 7 8 9 a b c d e f 10 11 12 13
  //   14 15 16 17 18 19 1a 1b 1c 1d 1e 1f 20 21 22 23 24 25 26 27 28 29 2a 2b 2c 2d 2e 2f 30 31 32 33 34
  //   35 36 37 38 39 3a 3b 3c 3d 3e 3f 40 41 42 43 44 45 46 47 48 49 4a 4b 4c 4d 4e 4f 50 51 52 53 54 55
  //   56 57 58 59 5a 5b 5c 5d 5e 5f 60 61 62 63 64 65 66 67 68 69 6a 6b 6c 6d 6e 6f 70 71 72 73 74 75 76
  //   77 78 79 7a 7b 7c 7d 7e 7f 80 81 82 83 84 85 86 87 88 89 8a 8b 8c 8d 8e 8f 90 91 92 93 94 95 96 97
  //   98 99 9a 9b 9c 9d 9e 9f a0 a1 a2 a3 a4 a5 a6 a7 a8 a9 aa ab ac ad ae af b0 b1 b2 b3 b4 b5 b6 b7 b8
  //   b9 ba bb bc bd be bf c0 c1 c2 c3 c4 c5 c6 c7 c8 c9 ca cb cc cd ce cf d0 d1 d2 d3 d4 d5 d6 d7 d8 d9
  //   da db dc dd de df e0 e1 e2 e3 e4 e5 e6 e7 e8 e9 ea eb ec ed ee ef f0 f1 f2 f3 f4 f5 f6 f7 f8 f9 fa
  //   fb fc fd fe ff 0 1 2 3 4 5 6 7 8 9 a b c d e f 10 11 12 13 14 15 16 17 18 19 1a 1b 1c 1d 1e 1f 20 21
  //   22 23 24 25 26 27 28 29 2a 2b 2c 2d 2e 2f 30 31 32 33 34 35 36 37 38 39 3a 3b 3c 3d 3e 3f 40 41 42
  //   43 44 45 46 47 48 49 4a 4b 4c 4d 4e 4f 50 51 52 53 54 55 56 57 58 59 5a 5b 5c 5d 5e 5f 60 61 62 63
  //   64 65 66 67 68 69 6a 6b 6c 6d 6e 6f 70 71 72 73 74 75 76 77 78 79 7a 7b 7c 7d 7e 7f 80 81 82 83 84
  //   85 86 87 88 89 8a 8b 8c 8d 8e 8f 90 91 92 93 94 95 96 97 98 99 9a 9b 9c 9d 9e 9f a0 a1 a2 a3 a4 a5
  //   a6 a7 a8 a9 aa ab ac ad ae af b0 b1 b2 b3 b4 b5 b6 b7 b8 b9 ba bb bc bd be bf c0 c1 c2 c3 c4 c5 c6
  //   c7 c8 c9 ca cb cc cd ce cf d0 d1 d2 d3 d4 d5 d6 d7 d8 d9 da db dc dd de df e0 e1 e2 e3 e4 e5 e6 e7
  //   e8 e9 ea eb ec ed ee ef f0 f1 f2 f3 f4 f5 f6 f7 f8 f9 fa fb fc fd fe ff 0 1 2 3 4 5 6 7 8 9 a b c d
  //   e f 10 11 12 13 14 15 16 17 18 19 1a 1b 1c 1d 1e 1f 20 21 22 23 24 25 26 27 28 29 2a 2b 2c 2d 2e 2f
  //   30 31 32 33 34 35 36 37 38 39 3a 3b 3c 3d 3e 3f 40 41 42 43 44 45 46 47 48 49 4a 4b 4c 4d 4e 4f 50
  //   51 52 53 54 55 56 57 58 59 5a 5b 5c 5d 5e 5f 60 61 62 63 64 65 66 67 68 69 6a 6b 6c 6d 6e 6f 70 71
  //   72 73 74 75 76 77 78 79 7a 7b 7c 7d 7e 7f 80 81 82 83 84 85 86 87 88 89 8a 8b 8c 8d 8e 8f 90 91 92
  //   93 94 95 96 97 98 99 9a 9b 9c 9d 9e 9f a0 a1 a2 a3 a4 a5 a6 a7 a8 a9 aa ab ac ad ae af b0 b1 b2 b3
  //   b4 b5 b6 b7 b8 b9 ba bb bc bd be bf c0 c1 c2 c3 c4 c5 c6 c7 c8 c9 ca cb cc cd ce cf d0 d1 d2 d3 d4
  //   d5 d6 d7 d8 d9 da db dc dd de df e0 e1 e2 e3 e4 e5 e6 e7 e8 e9 ea eb ec ed ee ef f0 f1 f2 f3 f4 f5
  //   f6 f7 f8 f9 fa fb fc fd fe ff 0 1 2 3 4 5 6 7 8 9 a b c d e f 10 11 12 13 14 15 16 17 18 19 1a 1b 1c
  //   1d 1e 1f 20 21 22 23 24 25 26 27 28 29 2a 2b 2c 2d 2e 2f 30 31 32 33 34 35 36 37 38 39 3a 3b 3c 3d
  //   3e 3f 40 41 42 43 44 45 46 47 48 49 4a 4b 4c 4d 4e 4f 50 51 52 53 54 55 56 57 58 59 5a 5b 5c 5d 5e
  //   5f 60 61 62 63 64 65 66 67 68 69 6a 6b 6c 6d 6e 6f 70 71 72 73 74 75 76 77 78 79 7a 7b 7c 7d 7e 7f
  //   80 81 82 83 84 85 86 87 88 89 8a 8b 8c 8d 8e 8f 90 91 92 93 94 95 96 97 98 99 9a 9b 9c 9d 9e 9f a0
  //   a1 a2 a3 a4 a5 a6 a7 a8 a9 aa ab ac ad ae af b0 b1 b2 b3 b4 b5 b6 b7 b8 b9 ba bb bc bd be bf c0 c1
  //   c2 c3 c4 c5 c6 c7 c8 c9 ca cb cc cd ce cf d0 d1 d2 d3 d4 d5 d6 d7 d8 d9 da db dc dd de df e0 e1 e2
  //   e3 e4 e5 e6 e7 e8 e9 ea eb ec ed ee ef f0 f1 f2 f3 f4 f5 f6 f7 f8 f9 fa fb fc fd fe ff
  //   cache模拟器
endmodule
