// Logisim project 寄存器文件设计实验.circ as structural Verilog: 4 circuits, main circuit 寄存器文件电路（4个寄存器）
// 寄存器文件电路
module \寄存器文件电路_4个寄存器  (
  input  [1:0] in_1,
  input  [1:0] in_2,
  input  [31:0] in_3,
  input  [1:0] in_4,
  input  in_5,
  input  in_6,
  output [31:0] out_7,
  output [31:0] out_8
);

  wire and_1_out, and_2_out, and_3_out, and_4_out, decoder_1_out0, decoder_1_out1, decoder_1_out2,
       decoder_1_out3;
  wire [31:0] register_1_q, register_2_q, register_3_q, register_4_q;

  Decoder #(.select(2), .enable("false")) decoder_1 (
    .out0(decoder_1_out0), .out1(decoder_1_out1), .out2(decoder_1_out2), .out3(decoder_1_out3), .sel(in_4));
  and and_1 (and_1_out, in_5, decoder_1_out0);
  and and_2 (and_2_out, decoder_1_out1, in_5);
  and and_3 (and_3_out, decoder_1_out2, in_5);
  and and_4 (and_4_out, decoder_1_out3, in_5);
  Register #(.width(32), .Select("low")) register_1 (
    .D(in_3), .en(and_1_out), .Q(register_1_q), .clk(in_6));  // open: clr
  Register #(.width(32), .Select("low")) register_2 (
    .D(in_3), .en(and_2_out), .Q(register_2_q), .clk(in_6));  // open: clr
  Register #(.width(32), .Select("low")) register_3 (
    .D(in_3), .en(and_3_out), .Q(register_3_q), .clk(in_6));  // open: clr
  Register #(.width(32), .Select("low")) register_4 (
    .D(in_3), .en(and_4_out), .Q(register_4_q), .clk(in_6), .clr(in_6));
  Multiplexer #(.select(2), .width(32), .enable("false")) multiplexer_1 (
    .in0(register_1_q), .in1(register_2_q), .in2(register_3_q), .in3(register_4_q), .out(out_7), .sel(in_1));
  Multiplexer #(.select(2), .width(32), .enable("false")) multiplexer_2 (
    .in0(register_1_q), .in1(register_2_q), .in2(register_3_q), .in3(register_4_q), .out(out_8), .sel(in_2));

  // Other names for the same wires on the sheet: CLK = in_6; Din[31:0] = in_3; R1_num[1:0] = in_1; R2_num[1:0] = in_2;
  //   RD1[31:0] = out_7; RD2[31:0] = out_8; W_num[1:0] = in_4; WE = in_5

  // Notes on the sheet:
  //   输入引脚
  //   请同学们在此设计电路！
  //   寄存器文件电路（4个寄存器）
  //   输出引脚
endmodule

// 寄存器文件电路(R0=0)
module \寄存器文件电路_4个寄存器_R0_0  (
  input  [1:0] in_1,
  input  [1:0] in_2,
  input  [31:0] in_3,
  input  [1:0] in_4,
  input  in_5,
  input  in_6,
  output [31:0] out_7,
  output [31:0] out_8
);

  wire and_1_out, and_2_out, and_3_out, and_4_out, decoder_1_out0, decoder_1_out1, decoder_1_out2,
       decoder_1_out3;
  wire [31:0] register_1_q, register_2_q, register_3_q, register_4_q;

  Decoder #(.select(2), .enable("false")) decoder_1 (
    .out0(decoder_1_out0), .out1(decoder_1_out1), .out2(decoder_1_out2), .out3(decoder_1_out3), .sel(in_4));
  and and_1 (and_1_out, in_5, decoder_1_out0);
  and and_2 (and_2_out, decoder_1_out1, in_5);
  and and_3 (and_3_out, decoder_1_out2, in_5);
  and and_4 (and_4_out, decoder_1_out3, in_5);
  Register #(.width(32), .Select("low")) register_1 (
    .D({32{1'b0}}), .en(and_1_out), .Q(register_1_q), .clk(in_6));  // open: clr
  Register #(.width(32), .Select("low")) register_2 (
    .D(in_3), .en(and_2_out), .Q(register_2_q), .clk(in_6));  // open: clr
  Register #(.width(32), .Select("low")) register_3 (
    .D(in_3), .en(and_3_out), .Q(register_3_q), .clk(in_6));  // open: clr
  Register #(.width(32), .Select("low")) register_4 (
    .D(in_3), .en(and_4_out), .Q(register_4_q), .clk(in_6), .clr(in_6));
  Multiplexer #(.select(2), .width(32), .enable("false")) multiplexer_1 (
    .in0(register_1_q), .in1(register_2_q), .in2(register_3_q), .in3(register_4_q), .out(out_7), .sel(in_1));
  Multiplexer #(.select(2), .width(32), .enable("false")) multiplexer_2 (
    .in0(register_1_q), .in1(register_2_q), .in2(register_3_q), .in3(register_4_q), .out(out_8), .sel(in_2));

  // Other names for the same wires on the sheet: CLK = in_6; Din[31:0] = in_3; R1_num[1:0] = in_1; R2_num[1:0] = in_2;
  //   RD1[31:0] = out_7; RD2[31:0] = out_8; W_num[1:0] = in_4; WE = in_5

  // Notes on the sheet:
  //   输入引脚
  //   请同学们在此设计电路！
  //   寄存器文件电路（4个寄存器，R0=0）
  //   输出引脚
endmodule

module \寄存器文件测试电路  (
  input  [1:0] R1_num,
  input  [1:0] R2_num,
  input  [1:0] W_num,
  input  WE,
  input  [31:0] Din,
  output [31:0] RD1,
  output [31:0] RD2
);

  wire CLK_out;

  \寄存器文件电路_4个寄存器  \u_寄存器文件电路_4个寄存器_1  (
    .in_1(R1_num), .in_2(R2_num), .in_3(Din), .in_4(W_num), .in_5(WE), .in_6(CLK_out), .out_7(RD1),
    .out_8(RD2));
  // Probe on Din
  Clock CLK (.out(CLK_out));
  // Probe on RD1
  // Probe on RD2

  // Notes on the sheet:
  //   R1#
  //   R2#
  //   W#
  //   WE
  //   Din
  //   RD1
  //   RD2
  //   CLK
  //   简单的寄存器文件测试电路
endmodule

module \寄存器文件测试电路_R0_0  (
  input  [1:0] R1_num,
  input  [1:0] R2_num,
  input  [1:0] W_num,
  input  WE,
  input  [31:0] Din,
  output [31:0] RD1,
  output [31:0] RD2
);

  wire CLK_out;

  \寄存器文件电路_4个寄存器_R0_0  \u_寄存器文件电路_4个寄存器_r0_0_1  (
    .in_1(R1_num), .in_2(R2_num), .in_3(Din), .in_4(W_num), .in_5(WE), .in_6(CLK_out), .out_7(RD1),
    .out_8(RD2));
  // Probe on Din
  Clock CLK (.out(CLK_out));
  // Probe on RD1
  // Probe on RD2

  // Notes on the sheet:
  //   R1#
  //   R2#
  //   W#
  //   Din
  //   WE
  //   RD1
  //   RD2
  //   CLK
  //   简单的寄存器文件测试电路（R0=0）
endmodule
