// Logisim project 8位循环冗余校验码（并行）实验.circ as structural Verilog: 3 circuits, main circuit CRC码传输测试实验1
module \CRC码传输测试实验1  (
  input  [7:0] \原始数据 
);

  wire CLK_out, comparator_1_eq, \crc并行解码电路_1__1位错 , \crc并行解码电路_1__2位错 , \crc并行解码电路_1_无错误 , \随机干扰电路_1_p2 ;
  wire [7:0] \crc并行解码电路_1_纠错后数据 ;
  wire [12:0] \crc并行编码电路_1_crc校验码 , \随机干扰电路_1_p4 ;

  // Probe on \原始数据 
  // Probe on \crc并行编码电路_1_crc校验码 
  \CRC并行编码电路  \crc并行编码电路_1  (.\原始数据 (\原始数据 ), .\CRC校验码 (\crc并行编码电路_1_crc校验码 ));
  // Probe on \随机干扰电路_1_p2 
  Clock CLK (.out(CLK_out));
  // 随机干扰电路 随机干扰电路_1: pin names not known; wires that end beside it: \crc并行编码电路_1_crc校验码 , \随机干扰电路_1_p2 , CLK_out, \随机干扰电路_1_p4 
  // Probe on \随机干扰电路_1_p4 
  LED \u_无错  (.in(\crc并行解码电路_1_无错误 ));
  LED \_1位错  (.in(\crc并行解码电路_1__1位错 ));
  LED \_2位错  (.in(\crc并行解码电路_1__2位错 ));
  \CRC并行解码电路  \crc并行解码电路_1  (
    .\CRC编码 (\随机干扰电路_1_p4 ), .\无错误 (\crc并行解码电路_1_无错误 ), .\_1位错 (\crc并行解码电路_1__1位错 ),
    .\_2位错 (\crc并行解码电路_1__2位错 ), .\纠错后数据 (\crc并行解码电路_1_纠错后数据 ));
  // Probe on \crc并行解码电路_1_纠错后数据 
  Comparator comparator_1 (.a(\原始数据 ), .b(\crc并行解码电路_1_纠错后数据 ), .eq(comparator_1_eq));  // open: gt, lt
  LED \u_数据正确  (.in(comparator_1_eq));

  // Notes on the sheet:
  //   发送方
  //   电路功能：测试CRC编解码电路正确性
  //   1、无错：无错灯红色，数据正确灯红色，接收数据等于发送数据
  //   先设置原始数据，然后每按“CLK”按钮2次，产生1个随机干扰，观看4个指示灯，有4种情况：
  //   2、1位错：1位错灯红色，数据正确灯红色，接收数据等于发送数据（可以纠正1位错）
  //   3、2位错：2位错灯红色，数据正确灯白色，接收数据不等于发送数据（不能纠正1位错）
  //   4、2位错：2位错灯红色，数据正确灯红色，接收数据等于发送数据（可以纠正某些情况的2位错误）
  //   输入：8位原始数据             输出：8位解码后的数据，4个指示灯（无错、1位错、2位错、数据正确）
  //   CRC码传输测试实验1
  //   接收方
endmodule

// CRC编码
module \CRC并行编码电路  (
  input  [7:0] \原始数据 ,
  output [12:0] \CRC校验码 
);

  wire [3:0] multiplexer_1_out, multiplexer_2_out, multiplexer_3_out, multiplexer_4_out, multiplexer_5_out,
       multiplexer_6_out, multiplexer_7_out, multiplexer_8_out;

  assign \CRC校验码 [3:0] = multiplexer_1_out ^ multiplexer_2_out ^ multiplexer_3_out ^ multiplexer_5_out ^ multiplexer_6_out ^ multiplexer_7_out ^ multiplexer_8_out ^ multiplexer_4_out;  // XOR_Gate xor_1, 4 bits wide
  Multiplexer #(.width(4)) multiplexer_1 (
    .in0(4'b0000), .in1(4'b1110), .out(multiplexer_1_out), .sel(\原始数据 [7]));  // open: en
  Multiplexer #(.width(4)) multiplexer_2 (
    .in0(4'b0000), .in1(4'b0111), .out(multiplexer_2_out), .sel(\原始数据 [6]));  // open: en
  Multiplexer #(.width(4)) multiplexer_3 (
    .in0(4'b0000), .in1(4'b0001), .out(multiplexer_3_out), .sel(\原始数据 [5]));  // open: en
  Multiplexer #(.width(4)) multiplexer_4 (
    .in0(4'b0000), .in1(4'b1010), .out(multiplexer_4_out), .sel(\原始数据 [4]));  // open: en
  Multiplexer #(.width(4)) multiplexer_5 (
    .in0(4'b0000), .in1(4'b1101), .out(multiplexer_5_out), .sel(\原始数据 [3]));  // open: en
  Multiplexer #(.width(4)) multiplexer_6 (
    .in0(4'b0000), .in1(4'b0100), .out(multiplexer_6_out), .sel(\原始数据 [2]));  // open: en
  Multiplexer #(.width(4)) multiplexer_7 (
    .in0(4'b0000), .in1(4'b1010), .out(multiplexer_7_out), .sel(\原始数据 [1]));  // open: en
  Multiplexer #(.width(4)) multiplexer_8 (
    .in0(4'b0000), .in1(4'b0101), .out(multiplexer_8_out), .sel(\原始数据 [0]));  // open: en
  xor xor_2 (\CRC校验码 [12], \CRC校验码 [0], \CRC校验码 [1], \原始数据 [0], \原始数据 [1], \原始数据 [2], \原始数据 [3], \原始数据 [5], \原始数据 [6], \原始数据 [7], \CRC校验码 [2], \原始数据 [4], \CRC校验码 [3]);

  assign \CRC校验码 [11:4] = \原始数据 ;

  // Other names for the same wires on the sheet: CRC编码[12:0] = {\CRC校验码 [12], \原始数据 , \CRC校验码 [3:0]};
  //   P1 = \CRC校验码 [0]; P2 = \CRC校验码 [1]; P3 = \CRC校验码 [2]; P4 = \CRC校验码 [3]; D1 = \原始数据 [0]; D2 = \原始数据 [1];
  //   D3 = \原始数据 [2]; D4 = \原始数据 [3]; D5 = \原始数据 [4]; D6 = \原始数据 [5]; D7 = \原始数据 [6]; D8 = \原始数据 [7];
  //   P5 = \CRC校验码 [12]

  // Notes on the sheet:
  //   电路功能：循环冗余校验编码电路                生成多项式=100101
  //   输入引脚区
  //   CRC并行编码电路
  //   输出引脚区
  //   输入：8位原始数据                             输出：13位循环冗余校验码（8位数据位+5位校验位）
endmodule

// CRC解码
module \CRC并行解码电路  (
  input  [12:0] \CRC编码 ,
  output \无错误 ,
  output \_1位错 ,
  output \_2位错 ,
  output [7:0] \纠错后数据 
);

  wire and_2_out, nor_1_out, xor_1_out, xor_2_out;
  wire [3:0] multiplexer_2_out, multiplexer_3_out, multiplexer_4_out, multiplexer_5_out, multiplexer_7_out,
       multiplexer_8_out, multiplexer_9_out, multiplexer_10_out, xor_3_out;
  wire [7:0] and_4_out, multiplexer_1_out, multiplexer_6_out;

  and and_1 (\_2位错 , ~xor_2_out, ~nor_1_out);  // AND_Gate
  xor xor_1 (xor_1_out, \CRC编码 [0], \CRC编码 [1], \CRC编码 [4], \CRC编码 [5], \CRC编码 [6], \CRC编码 [7], \CRC编码 [9], \CRC编码 [10], \CRC编码 [11], \CRC编码 [2], \CRC编码 [8], \CRC编码 [3]);
  xor xor_2 (xor_2_out, xor_1_out, \CRC编码 [12]);
  or or_1 (\_1位错 , xor_2_out, and_2_out);
  and and_2 (and_2_out, xor_2_out, ~nor_1_out);  // AND_Gate
  and and_3 (\无错误 , ~xor_2_out, nor_1_out);  // AND_Gate
  nor nor_1 (nor_1_out, xor_3_out[3], xor_3_out[2], xor_3_out[1], xor_3_out[0]);
  Multiplexer #(.select(4), .width(8)) multiplexer_1 (
    .in0({8{1'b0}}), .in1({8{1'b0}}), .in2({8{1'b0}}), .in3({8{1'b0}}), .in4({8{1'b0}}), .in5(8'h1),
    .in6({8{1'b0}}), .in7(8'h40), .in8({8{1'b0}}), .in9({8{1'b0}}), .in10(8'h2), .in11({8{1'b0}}),
    .in12({8{1'b0}}), .in13(8'h8), .in14(8'h80), .in15({8{1'b0}}), .out(multiplexer_1_out), .sel(xor_3_out),
    .en(1'b1));
  assign xor_3_out = \CRC编码 [3:0] ^ multiplexer_2_out ^ multiplexer_4_out ^ multiplexer_3_out ^ multiplexer_7_out ^ multiplexer_5_out ^ multiplexer_8_out ^ multiplexer_9_out ^ multiplexer_10_out;  // XOR_Gate xor_3, 4 bits wide
  Multiplexer #(.width(4)) multiplexer_2 (
    .in0(4'b0000), .in1(4'b1110), .out(multiplexer_2_out), .sel(\CRC编码 [11]));  // open: en
  Multiplexer #(.width(4)) multiplexer_3 (
    .in0(4'b0000), .in1(4'b0001), .out(multiplexer_3_out), .sel(\CRC编码 [9]));  // open: en
  Multiplexer #(.width(4)) multiplexer_4 (
    .in0(4'b0000), .in1(4'b0111), .out(multiplexer_4_out), .sel(\CRC编码 [10]));  // open: en
  Multiplexer #(.width(4)) multiplexer_5 (
    .in0(4'b0000), .in1(4'b1010), .out(multiplexer_5_out), .sel(\CRC编码 [8]));  // open: en
  Multiplexer #(.width(8)) multiplexer_6 (
    .in0({8{1'b0}}), .in1({8{1'b1}}), .out(multiplexer_6_out), .sel(\_1位错 ));  // open: en
  Multiplexer #(.width(4)) multiplexer_7 (
    .in0(4'b0000), .in1(4'b1101), .out(multiplexer_7_out), .sel(\CRC编码 [7]));  // open: en
  Multiplexer #(.width(4)) multiplexer_8 (
    .in0(4'b0000), .in1(4'b0100), .out(multiplexer_8_out), .sel(\CRC编码 [6]));  // open: en
  assign and_4_out = multiplexer_6_out & multiplexer_1_out;  // AND_Gate and_4, 8 bits wide
  Multiplexer #(.width(4)) multiplexer_9 (
    .in0(4'b0000), .in1(4'b1010), .out(multiplexer_9_out), .sel(\CRC编码 [5]));  // open: en
  Multiplexer #(.width(4)) multiplexer_10 (
    .in0(4'b0000), .in1(4'b0101), .out(multiplexer_10_out), .sel(\CRC编码 [4]));  // open: en
  assign \纠错后数据  = \CRC编码 [11:4] ^ and_4_out;  // XOR_Gate xor_4, 8 bits wide

  // Other names for the same wires on the sheet: CRC[12:0] = \CRC编码 ; P1 = \CRC编码 [0]; P2 = \CRC编码 [1];
  //   P3 = \CRC编码 [2]; P4 = \CRC编码 [3]; D1 = \CRC编码 [4]; D2 = \CRC编码 [5]; D3 = \CRC编码 [6]; D4 = \CRC编码 [7];
  //   D5 = \CRC编码 [8]; D6 = \CRC编码 [9]; D7 = \CRC编码 [10]; D8 = \CRC编码 [11]; P5 = \CRC编码 [12]

  // Notes on the sheet:
  //   电路功能：实现13位CRC编码的数据解码，能判断无错误、1位错、2位错，1位错具有自动纠错功能        生成多项式=100101
  //   输入引脚区
  //   CRC并行解码电路
  //   输出引脚区
  //   输入：13位CRC编码    输出：8位纠错后的数据，错误标志（无错误、1位错、2位错）
endmodule
