// Logisim project 原码和补码一位乘法器.circ as structural Verilog: 7 circuits, main circuit 1位全加器（FA）
// 8位无符号一位乘法器
module \_8位无符号数一位乘法器  (
  input  [7:0] X,
  input  [7:0] Y,
  output [15:0] \乘积 
);

  wire CLK, comparator_1_eq, d_ff_1_q, END, not_1_out, RST;
  wire [0:0] \n8位串行加法器_1_s ;
  wire [3:0] counter_1_q;
  wire [7:0] multiplexer_1_out, multiplexer_2_out, \n8位串行加法器_1_cout ;

  Button \u_复位  (.out(RST));
  // Probe on \乘积 [15:8]
  Register #(.Select("low")) register_1 (.D(\n8位串行加法器_1_cout ), .en(not_1_out), .Q(\乘积 [15:8]), .clk(CLK), .clr(RST));
  \_8位串行加法器  \u_8位串行加法器_1  (
    .X(\乘积 [15:8]), .Y(multiplexer_1_out), .Cin(1'b0), .S({\n8位串行加法器_1_cout [6:0], \n8位串行加法器_1_s [0]}),
    .Cout(\n8位串行加法器_1_cout [7]));  // open: out_6
  Multiplexer #(.width(8), .enable("false")) multiplexer_1 (
    .in0({8{1'b0}}), .in1(X), .out(multiplexer_1_out), .sel(\乘积 [0]));
  Button u_CLK (.out(CLK));
  Multiplexer #(.width(8), .enable("false")) multiplexer_2 (
    .in0(Y), .in1({\n8位串行加法器_1_s [0], \乘积 [7:1]}), .out(multiplexer_2_out), .sel(d_ff_1_q));
  // Probe on \乘积 [7:0]
  Register #(.Select("low")) Y_2 (.D(multiplexer_2_out), .en(not_1_out), .Q(\乘积 [7:0]), .clk(CLK), .clr(RST));
  Counter #(.width(4), .max('hf), .behavior("old")) counter_1 (
    .count(not_1_out), .Q(counter_1_q), .clk(CLK), .clr(RST));  // open: load, D, carry, preset
  D_Flip_Flop #(.Pre_Clr_Positions("LEGACY"), .enable("true"), .NewFFLayout("false")) d_ff_1 (
    .clk(CLK), .D(1'b1), .Q(d_ff_1_q), .reset(RST));  // open: Qn, preset, en
  not not_1 (not_1_out, comparator_1_eq);
  Comparator #(.width(4), .mode("unsigned")) comparator_1 (
    .a(counter_1_q), .b(4'b1001), .eq(comparator_1_eq));  // open: gt, lt
  LED led_1 (.in(END));
  not not_2 (END, not_1_out);
  // Probe on X
  // Probe on Y
  // Probe on \乘积 

  // Notes on the sheet:
  //   输入引脚区
  //   ∑
  //   功能说明: 8位无符号数一位乘法器                输入：X、Y 为8位无符号数               输出：乘积=X*Y 为16位无符号数
  //   首先设置X、Y值，然后按“复位”按钮，接下去按“CLK”按钮多次，直到“END”指示灯变红，此时观看乘积是不是正确？
  //   8位无符号数一位乘法器
  //   输出引脚区
  //   ×
  //   =
endmodule

module \_8位原码一位乘法器  (
  input  [7:0] X,
  input  [7:0] Y,
  output [15:0] \乘积 
);

  wire _0, CLK, comparator_1_eq, d_ff_1_q, END, nor_1_out, nor_2_out, not_1_out, RST;
  wire [0:0] \n8位串行加法器_1_s ;
  wire [3:0] counter_1_q;
  wire [6:0] negator_1_out, negator_2_out, \X真值 , \Y真值 ;
  wire [7:0] multiplexer_1_out, multiplexer_2_out, \n8位串行加法器_1_cout ;
  wire [14:0] multiplexer_5_out, negator_3_out;
  wire [15:0] \乘积真值 ;
  wire [15:15] P;

  xor xor_1 (\乘积 [15], X[7], Y[7]);
  Button \u_复位  (.out(RST));
  Button u_CLK (.out(CLK));
  // Probe on {P[15], \乘积 [14:8]}
  Register #(.Select("low")) register_1 (
    .D(\n8位串行加法器_1_cout ), .en(not_1_out), .Q({P[15], \乘积 [14:8]}), .clk(CLK), .clr(RST));
  \_8位串行加法器  \u_8位串行加法器_1  (
    .X({P[15], \乘积 [14:8]}), .Y(multiplexer_1_out), .Cin(1'b0),
    .S({\n8位串行加法器_1_cout [6:0], \n8位串行加法器_1_s [0]}), .Cout(\n8位串行加法器_1_cout [7]));  // open: out_6
  Multiplexer #(.width(8), .enable("false")) multiplexer_1 (
    .in0({8{1'b0}}), .in1({1'b0, X[6:0]}), .out(multiplexer_1_out), .sel(\乘积 [0]));
  Multiplexer #(.width(8), .enable("false")) multiplexer_2 (
    .in0({1'b0, Y[6:0]}), .in1({\n8位串行加法器_1_s [0], \乘积 [7:1]}), .out(multiplexer_2_out), .sel(d_ff_1_q));
  // Probe on \乘积 [7:0]
  Register #(.Select("low")) Y_2 (.D(multiplexer_2_out), .en(not_1_out), .Q(\乘积 [7:0]), .clk(CLK), .clr(RST));
  Counter #(.width(4), .max('hf), .behavior("old")) counter_1 (
    .count(not_1_out), .Q(counter_1_q), .clk(CLK), .clr(RST));  // open: load, D, carry, preset
  D_Flip_Flop #(.Pre_Clr_Positions("LEGACY"), .enable("true"), .NewFFLayout("false")) d_ff_1 (
    .clk(CLK), .D(1'b1), .Q(d_ff_1_q), .reset(RST));  // open: Qn, preset, en
  LED led_1 (.in(END));
  not not_1 (not_1_out, comparator_1_eq);
  Comparator #(.width(4), .mode("unsigned")) comparator_1 (
    .a(counter_1_q), .b(4'b1001), .eq(comparator_1_eq));  // open: gt, lt
  Negator #(.width(7)) negator_1 (.in(X[6:0]), .out(negator_1_out));
  not not_2 (END, not_1_out);
  // Probe on \乘积真值 
  Multiplexer #(.width(7), .enable("false")) multiplexer_3 (.in0(X[6:0]), .in1(negator_1_out), .out(\X真值 ), .sel(X[7]));
  Negator #(.width(7)) negator_2 (.in(Y[6:0]), .out(negator_2_out));
  // Probe on {X[7], \X真值 }
  // Probe on {Y[7], \Y真值 }
  Multiplexer #(.width(7), .enable("false")) multiplexer_4 (.in0(Y[6:0]), .in1(negator_2_out), .out(\Y真值 ), .sel(Y[7]));
  nor nor_1 (nor_1_out, X[0], X[1], X[2], X[3], X[4], X[5], X[6], X[7]);
  nor nor_2 (nor_2_out, Y[0], Y[1], Y[2], Y[3], Y[4], Y[5], Y[6], Y[7]);
  Negator #(.width(15)) negator_3 (.in(\乘积 [14:0]), .out(negator_3_out));
  or or_1 (_0, nor_1_out, nor_2_out);
  Multiplexer #(.width(15), .enable("false")) multiplexer_5 (
    .in0(\乘积 [14:0]), .in1(negator_3_out), .out(multiplexer_5_out), .sel(\乘积 [15]));
  Multiplexer #(.width(16), .enable("false")) multiplexer_6 (
    .in0({\乘积 [15], multiplexer_5_out}), .in1({16{1'b0}}), .out(\乘积真值 ), .sel(_0));

  // Other names for the same wires on the sheet: P15 = \乘积 [15]; X6_0[6:0] = X[6:0]; X_t[6:0] = X[6:0]; X真值[7] = X[7];
  //   Y6_0[6:0] = Y[6:0]; Y_t[6:0] = Y[6:0]; Y真值[7] = Y[7]; P[14:0] = \乘积 [14:0]

  // Notes on the sheet:
  //   输入引脚区
  //   功能说明: 8位原码一位乘法器                输入：X、Y为 8位原码               输出：乘积=X*Y 为16位原码
  //   首先设置X、Y值，然后按“复位”按钮，接下去按“CLK”按钮多次，直到“END”指示灯变红，此时观看乘积是不是正确？
  //   ∑
  //   请同学们在此处设计电路！
  //   8位原码一位乘法器
  //   输出引脚区
  //   ×
  //   =
endmodule

module \_8位补码一位乘法器_简化版  (
  input  [7:0] X,
  input  [7:0] Y,
  output [15:0] \乘积 
);

  wire and_1_out, CLK, comparator_1_eq, comparator_2_eq, d_ff_1_q, END, not_3_out, RST;
  wire [0:0] \n8位串行加法器_1_s_2 ;
  wire [1:1] Yn_1_2_q;
  wire [3:0] counter_1_q;
  wire [7:0] multiplexer_1_out, multiplexer_2_out, \n8位串行加法器_1_s , not_1_out;
  wire [15:0] negator_1_out, \乘积_star ;

  Register #(.Select("low")) register (
    .D({{2{\n8位串行加法器_1_s [7]}}, \n8位串行加法器_1_s [5:0]}), .en(not_3_out), .Q(\乘积_star [15:8]), .clk(CLK),
    .clr(RST));
  assign not_1_out = ~X;  // NOT_Gate not_1, 8 bits wide
  // Probe on \乘积_star [15:8]
  Multiplexer #(.width(8), .enable("false")) multiplexer_1 (
    .in0(Y), .in1({\n8位串行加法器_1_s_2 [0], \乘积_star [7:1]}), .out(multiplexer_1_out), .sel(d_ff_1_q));
  \_8位串行加法器  \u_8位串行加法器_1  (
    .X(\乘积_star [15:8]), .Y(multiplexer_2_out), .Cin(and_1_out),
    .S({\n8位串行加法器_1_s [7], \n8位串行加法器_1_s [5:0], \n8位串行加法器_1_s_2 [0]}));  // open: Cout, out_6
  Multiplexer #(.select(2), .width(8), .enable("false")) multiplexer_2 (
    .in0({8{1'b0}}), .in1(not_1_out), .in2(X), .in3({8{1'b0}}), .out(multiplexer_2_out),
    .sel({Yn_1_2_q[1], \乘积_star [0]}));
  Button \u_复位  (.out(RST));
  // Probe on \乘积_star [7:0]
  Register #(.Select("low")) Y_2 (.D(multiplexer_1_out), .en(not_3_out), .Q(\乘积_star [7:0]), .clk(CLK), .clr(RST));
  and and_1 (and_1_out, ~Yn_1_2_q[1], \乘积_star [0]);  // AND_Gate
  Counter #(.width(4), .max('hf), .behavior("old")) counter_1 (
    .count(not_3_out), .Q(counter_1_q), .clk(CLK), .clr(RST));  // open: load, D, carry, preset
  // Probe on Yn_1_2_q[1]
  Register #(.width(1), .Select("low")) Yn_1_2 (
    .D(\乘积_star [0]), .en(not_3_out), .Q(Yn_1_2_q[1]), .clk(CLK), .clr(RST));
  Comparator #(.width(4), .mode("unsigned")) comparator_1 (
    .a(counter_1_q), .b(4'b1001), .eq(comparator_1_eq));  // open: gt, lt
  D_Flip_Flop #(.Pre_Clr_Positions("LEGACY"), .enable("true"), .NewFFLayout("false")) d_ff_1 (
    .clk(CLK), .D(1'b1), .Q(d_ff_1_q), .reset(RST));  // open: Qn, preset, en
  Button \u_时钟  (.out(CLK));
  not not_2 (END, not_3_out);
  not not_3 (not_3_out, comparator_1_eq);
  // Probe on \乘积_star 
  // Probe on \乘积_star 
  LED led_1 (.in(END));
  Negator #(.width(16)) negator_1 (.in(\乘积_star ), .out(negator_1_out));
  Comparator comparator_2 (.a(X), .b(8'h80), .eq(comparator_2_eq));  // open: gt, lt
  Multiplexer #(.width(16), .enable("false")) multiplexer_3 (
    .in0(\乘积_star ), .in1(negator_1_out), .out(\乘积 ), .sel(comparator_2_eq));
  // Probe on X
  // Probe on Y
  // Probe on \乘积 
  // Probe on \乘积 

  // Notes on the sheet:
  //   输入引脚区
  //   功能说明: 8位补码一位乘法器                输入：X、Y 为8位补码               输出：乘积=X*Y 为16位补码
  //   首先设置X、Y值，然后按“复位”按钮，接下去按“CLK”按钮多次，直到“END”指示灯变红，此时观看乘积是不是正确？
  //   8位补码一位乘法器（简化版）
  //   输出引脚区
  //   ×
  //   =
endmodule

module \_8位补码一位乘法器_复杂版  (
  input  [7:0] X,
  input  [7:0] Y,
  output [15:0] \乘积 
);

  wire and_1_out, CLK, comparator_1_eq, d_ff_1_q, END, not_3_out, RST, XYZ, XZ, YZ;
  wire [0:0] \n8位串行加法器_1_s_2 ;
  wire [1:0] PS;
  wire [1:1] Yn_1_2_q;
  wire [3:0] counter_1_q;
  wire [7:0] multiplexer_1_out, multiplexer_2_out, \n8位串行加法器_1_s , not_1_out;
  wire [14:0] PX_star, PY_star;
  wire [15:0] multiplexer_3_out, P_star;
  wire [15:15] negator_1_out, negator_2_out, PX;

  // Probe on X
  Register #(.Select("low")) register (
    .D({{2{\n8位串行加法器_1_s [7]}}, \n8位串行加法器_1_s [5:0]}), .en(not_3_out), .Q(P_star[15:8]), .clk(CLK), .clr(RST));
  assign not_1_out = ~X;  // NOT_Gate not_1, 8 bits wide
  // Probe on Y
  // Probe on P_star[15:8]
  Multiplexer #(.width(8), .enable("false")) multiplexer_1 (
    .in0(Y), .in1({\n8位串行加法器_1_s_2 [0], P_star[7:1]}), .out(multiplexer_1_out), .sel(d_ff_1_q));
  \_8位串行加法器  \u_8位串行加法器_1  (
    .X(P_star[15:8]), .Y(multiplexer_2_out), .Cin(and_1_out),
    .S({\n8位串行加法器_1_s [7], \n8位串行加法器_1_s [5:0], \n8位串行加法器_1_s_2 [0]}));  // open: Cout, out_6
  Multiplexer #(.select(2), .width(8), .enable("false")) multiplexer_2 (
    .in0({8{1'b0}}), .in1(not_1_out), .in2(X), .in3({8{1'b0}}), .out(multiplexer_2_out),
    .sel({Yn_1_2_q[1], P_star[0]}));
  Button \u_复位  (.out(RST));
  // Probe on P_star[7:0]
  Register #(.Select("low")) Y_2 (.D(multiplexer_1_out), .en(not_3_out), .Q(P_star[7:0]), .clk(CLK), .clr(RST));
  and and_1 (and_1_out, ~Yn_1_2_q[1], P_star[0]);  // AND_Gate
  Counter #(.width(4), .max('hf), .behavior("old")) counter_1 (
    .count(not_3_out), .Q(counter_1_q), .clk(CLK), .clr(RST));  // open: load, D, carry, preset
  // Probe on Yn_1_2_q[1]
  Register #(.width(1), .Select("low")) Yn_1_2 (.D(P_star[0]), .en(not_3_out), .Q(Yn_1_2_q[1]), .clk(CLK), .clr(RST));
  Comparator #(.width(4), .mode("unsigned")) comparator_1 (
    .a(counter_1_q), .b(4'b1001), .eq(comparator_1_eq));  // open: gt, lt
  D_Flip_Flop #(.Pre_Clr_Positions("LEGACY"), .enable("true"), .NewFFLayout("false")) d_ff_1 (
    .clk(CLK), .D(1'b1), .Q(d_ff_1_q), .reset(RST));  // open: Qn, preset, en
  Button \u_时钟  (.out(CLK));
  not not_2 (END, not_3_out);
  not not_3 (not_3_out, comparator_1_eq);
  // Probe on \乘积 
  xor xor_1 (XYZ, XZ, YZ);
  Negator #(.width(16)) negator_1 (.in({PX[15], X, {7{1'b0}}}), .out({negator_1_out[15], PX_star}));
  Comparator comparator_2 (.a(X), .b(8'h80), .eq(PS[0]));  // open: gt, lt
  Comparator comparator_3 (.a(Y), .b(8'h80), .eq(PS[1]));  // open: gt, lt
  or or_1 (XZ, X[0], X[1], X[2], X[3], X[4], X[5], X[6], X[7]);
  LED led_1 (.in(END));
  xor xor_2 (PX[15], X[7], Y[7]);
  Negator #(.width(16)) negator_2 (.in({PX[15], Y, {7{1'b0}}}), .out({negator_2_out[15], PY_star}));
  Multiplexer #(.select(2), .width(16), .enable("false")) multiplexer_3 (
    .in0(P_star), .in1({PX[15], PY_star}), .in2({PX[15], PX_star}), .in3(16'h4000), .out(multiplexer_3_out),
    .sel(PS));
  // Probe on X
  // Probe on Y
  // Probe on \乘积 
  or or_2 (YZ, Y[0], Y[1], Y[2], Y[3], Y[4], Y[5], Y[6], Y[7]);
  Multiplexer #(.width(16), .enable("false")) multiplexer_4 (
    .in0(multiplexer_3_out), .in1({16{1'b0}}), .out(\乘积 ), .sel(XYZ));

  // Other names for the same wires on the sheet: P[15:0] = \乘积 ; PX[14:7] = X; SX = X[7]; PY[15:7] = {PX[15], Y};
  //   SY = Y[7]; PX_star[15] = PX[15]; PY_star[15] = PX[15]; SP = PX[15]

  // Notes on the sheet:
  //   输入引脚区
  //   功能说明: 8位补码一位乘法器                输入：X、Y 为8位补码               输出：乘积=X*Y 为16位补码
  //   首先设置X、Y值，然后按“复位”按钮，接下去按“CLK”按钮多次，直到“END”指示灯变红，此时观看乘积是不是正确？
  //   8位补码一位乘法器（复杂版）
  //   输出引脚区
  //   ×
  //   =
endmodule

module \_8位补码一位乘法器_用8位无符号数一位乘法器实现  (
  input  [7:0] X,
  input  [7:0] Y,
  output [15:0] \乘积 
);

  wire _0, CLK, comparator_1_eq, comparator_2_eq, comparator_3_eq, d_ff_1_q, END, nor_1_out, nor_2_out,
       not_2_out, RST;
  wire [0:0] \n8位串行加法器_1_s ;
  wire [3:0] counter_1_q;
  wire [6:0] negator_1_out, negator_2_out, X_t, Y_t;
  wire [7:0] multiplexer_5_out, multiplexer_6_out, \n8位串行加法器_1_cout , Xm, Ym;
  wire [14:0] multiplexer_3_out, negator_3_out;
  wire [15:0] P;
  wire [15:15] P_t;

  // Probe on X
  nor nor_1 (nor_1_out, X[0], X[1], X[2], X[3], X[4], X[5], X[6], X[7]);
  nor nor_2 (nor_2_out, Y[0], Y[1], Y[2], Y[3], Y[4], Y[5], Y[6], Y[7]);
  or or_1 (_0, nor_1_out, nor_2_out);
  // Probe on Y
  Negator #(.width(7)) negator_1 (.in(X[6:0]), .out(negator_1_out));
  Negator #(.width(7)) negator_2 (.in(Y[6:0]), .out(negator_2_out));
  Negator #(.width(15)) negator_3 (.in(P[14:0]), .out(negator_3_out));
  Button \u_复位  (.out(RST));
  Multiplexer #(.width(7), .enable("false")) multiplexer_1 (.in0(X[6:0]), .in1(negator_1_out), .out(X_t), .sel(X[7]));
  Multiplexer #(.width(7), .enable("false")) multiplexer_2 (.in0(Y[6:0]), .in1(negator_2_out), .out(Y_t), .sel(Y[7]));
  xor xor_1 (P[15], X[7], Y[7]);
  Multiplexer #(.width(15), .enable("false")) multiplexer_3 (
    .in0(P[14:0]), .in1(negator_3_out), .out(multiplexer_3_out), .sel(P[15]));
  Button \u_时钟  (.out(CLK));
  Multiplexer #(.width(16), .enable("false")) multiplexer_4 (
    .in0({P[15], multiplexer_3_out}), .in1({16{1'b0}}), .out(\乘积 ), .sel(_0));
  // Probe on \乘积 
  // Probe on {P_t[15], P[14:8]}
  Register #(.Select("low")) register_1 (
    .D(\n8位串行加法器_1_cout ), .en(not_2_out), .Q({P_t[15], P[14:8]}), .clk(CLK), .clr(RST));
  Multiplexer #(.width(8), .enable("false")) multiplexer_5 (
    .in0(Ym), .in1({\n8位串行加法器_1_s [0], P[7:1]}), .out(multiplexer_5_out), .sel(d_ff_1_q));
  \_8位串行加法器  \u_8位串行加法器_1  (
    .X({P_t[15], P[14:8]}), .Y(multiplexer_6_out), .Cin(1'b0),
    .S({\n8位串行加法器_1_cout [6:0], \n8位串行加法器_1_s [0]}), .Cout(\n8位串行加法器_1_cout [7]));  // open: out_6
  Multiplexer #(.width(8), .enable("false")) multiplexer_6 (
    .in0({8{1'b0}}), .in1(Xm), .out(multiplexer_6_out), .sel(P[0]));
  LED led_1 (.in(END));
  // Probe on P[7:0]
  Register #(.Select("low")) Ym_2 (.D(multiplexer_5_out), .en(not_2_out), .Q(P[7:0]), .clk(CLK), .clr(RST));
  Counter #(.width(4), .max('hf), .behavior("old")) counter_1 (
    .count(not_2_out), .Q(counter_1_q), .clk(CLK), .clr(RST));  // open: load, D, carry, preset
  Comparator #(.width(4), .mode("unsigned")) comparator_1 (
    .a(counter_1_q), .b(4'b1001), .eq(comparator_1_eq));  // open: gt, lt
  D_Flip_Flop #(.Pre_Clr_Positions("LEGACY"), .enable("true"), .NewFFLayout("false")) d_ff_1 (
    .clk(CLK), .D(1'b1), .Q(d_ff_1_q), .reset(RST));  // open: Qn, preset, en
  // Probe on X
  // Probe on Y
  // Probe on \乘积 
  not not_1 (END, not_2_out);
  not not_2 (not_2_out, comparator_1_eq);
  Multiplexer #(.width(8), .enable("false")) multiplexer_7 (
    .in0({1'b0, X_t}), .in1(8'h80), .out(Xm), .sel(comparator_2_eq));
  Comparator comparator_2 (.a(X), .b(8'h80), .eq(comparator_2_eq));  // open: gt, lt
  Multiplexer #(.width(8), .enable("false")) multiplexer_8 (
    .in0({1'b0, Y_t}), .in1(8'h80), .out(Ym), .sel(comparator_3_eq));
  Comparator comparator_3 (.a(Y), .b(8'h80), .eq(comparator_3_eq));  // open: gt, lt

  // Other names for the same wires on the sheet: P_t[14:0] = P[14:0]; X6_0[6:0] = X[6:0]; X原码[7:0] = {X[7], X_t};
  //   Y6_0[6:0] = Y[6:0]; Y原码[7:0] = {Y[7], Y_t}

  // Notes on the sheet:
  //   输入引脚区
  //   首先设置X、Y值，然后按“复位”按钮，接下去按“CLK”按钮多次，直到“END”指示灯变红，此时观看乘积是不是正确？
  //   功能说明: 8位补码一位乘法器（用8位无符号数一位乘法器实现）                输入：X、Y 为8位补码               输出：乘积=X*Y 为16位补码
  //   请同学们在此处设计电路！
  //   8位补码一位乘法器（用8位无符号数一位乘法器实现）
  //   ∑
  //   输出引脚区
  //   ×
  //   =
endmodule

module \_8位串行加法器  (
  input  [7:0] X,
  input  [7:0] Y,
  input  Cin,
  output [7:0] S,
  output Cout,
  output out_6
);

  wire \n1位全加器_fa_2_cout , \n1位全加器_fa_3_cout , \n1位全加器_fa_4_cout , \n1位全加器_fa_5_cout , \n1位全加器_fa_6_cout ,
       \n1位全加器_fa_7_cout , \n1位全加器_fa_8_cout ;

  xor xor_1 (out_6, Cout, \n1位全加器_fa_2_cout );
  \_1位全加器_FA  \u_1位全加器_fa_1  (.Cout(Cout), .Si(S[7]), .Cin(\n1位全加器_fa_2_cout ), .Xi(X[7]), .Yi(Y[7]));
  \_1位全加器_FA  \u_1位全加器_fa_2  (.Cout(\n1位全加器_fa_2_cout ), .Si(S[6]), .Cin(\n1位全加器_fa_3_cout ), .Xi(X[6]), .Yi(Y[6]));
  \_1位全加器_FA  \u_1位全加器_fa_3  (.Cout(\n1位全加器_fa_3_cout ), .Si(S[5]), .Cin(\n1位全加器_fa_4_cout ), .Xi(X[5]), .Yi(Y[5]));
  \_1位全加器_FA  \u_1位全加器_fa_4  (.Cout(\n1位全加器_fa_4_cout ), .Si(S[4]), .Cin(\n1位全加器_fa_5_cout ), .Xi(X[4]), .Yi(Y[4]));
  \_1位全加器_FA  \u_1位全加器_fa_5  (.Cout(\n1位全加器_fa_5_cout ), .Si(S[3]), .Cin(\n1位全加器_fa_6_cout ), .Xi(X[3]), .Yi(Y[3]));
  \_1位全加器_FA  \u_1位全加器_fa_6  (.Cout(\n1位全加器_fa_6_cout ), .Si(S[2]), .Cin(\n1位全加器_fa_7_cout ), .Xi(X[2]), .Yi(Y[2]));
  // Probe on X
  // Probe on Y
  // Probe on S
  \_1位全加器_FA  \u_1位全加器_fa_7  (.Cout(\n1位全加器_fa_7_cout ), .Si(S[1]), .Cin(\n1位全加器_fa_8_cout ), .Xi(X[1]), .Yi(Y[1]));
  // Probe on X
  // Probe on Y
  // Probe on S
  \_1位全加器_FA  \u_1位全加器_fa_8  (.Cout(\n1位全加器_fa_8_cout ), .Si(S[0]), .Cin(Cin), .Xi(X[0]), .Yi(Y[0]));

  // Other names for the same wires on the sheet: OF = out_6

  // Notes on the sheet:
  //   Cin: pull=down
  //   X: pull=down
  //   Y: pull=down
  //   输入引脚区
  //   符号位
  //   输出引脚区
  //   8位串行加法器
  //   OF
  //   +
  //   有符号加法
  //   +
  //   =
  //   无符号加法
endmodule

// FA
module \_1位全加器_FA  (
  input  Cin,
  input  Xi,
  input  Yi,
  output Cout,
  output Si
);

  wire AND_2_out, AND_out, XOR_2_out;

  and AND (AND_out, Xi, Yi);
  or OR (Cout, AND_out, AND_2_out);
  and AND_2 (AND_2_out, Cin, XOR_2_out);
  xor XOR (Si, Cin, XOR_2_out);
  xor XOR_2 (XOR_2_out, Xi, Yi);

  // Notes on the sheet:
  //   Cin: pull=down
  //   Yi: pull=down
  //   Xi: pull=down
  //   Cout = Xi Yi + Cin (Xi ^ Yi)
  //   Si = Xi ^ Yi ^ Cin
  //   1位全加器（FA）
endmodule
